// Digital circuit 1.01.orSwitch.dig as structural Verilog
module _1_01_orSwitch (
);

  wire switch_1_b;

  Switch switch_1 (.A(1'b1), .B(switch_1_b));
  Switch switch_2 (.A(1'b1), .B(switch_1_b));
  LED led_1 (.in(switch_1_b));
endmodule
