// Digital circuit 1.02.andSwitch.dig as structural Verilog
module _1_02_andSwitch (
);

  wire switch_1_b, switch_2_b;

  Switch switch_1 (.A(1'b1), .B(switch_1_b));
  Switch switch_2 (.A(switch_1_b), .B(switch_2_b));
  LED led_1 (.in(switch_2_b));
endmodule
