// Digital circuit 1.03.notSwitch.dig as structural Verilog
module _1_03_notSwitch (
);

  wire switch_1_b;

  Switch switch_1 (.A(1'b0), .B(switch_1_b));
  PullUp pullup_1 (.out(switch_1_b));
  LED led_1 (.in(switch_1_b));
endmodule
