// Digital circuit 1.04.aoiSwitch.dig as structural Verilog
module _1_04_aoiSwitch (
);

  wire A_b, B_b, C_b;

  Switch A (.A(1'b0), .B(A_b));
  Switch C (.A(1'b0), .B(C_b));
  Switch B (.A(A_b), .B(B_b));
  Switch D (.A(C_b), .B(B_b));
  PullUp pullup_1 (.out(B_b));
  LED Z (.in(B_b));
endmodule
