// Digital circuit 1.05.aoiNMOS.dig as structural Verilog
module _1_05_aoiNMOS (
  input  B,
  input  A,
  input  D,
  input  C,
  output Z
);

  wire nfet_1_d, nfet_2_d;

  NFET nfet_1 (.G(A), .D(nfet_1_d), .S(1'b0));
  NFET nfet_2 (.G(C), .D(nfet_2_d), .S(1'b0));
  NFET nfet_3 (.G(B), .D(Z), .S(nfet_1_d));
  NFET nfet_4 (.G(D), .D(Z), .S(nfet_2_d));
  PullUp pullup_1 (.out(Z));
endmodule
