// Digital circuit 1.06.aoiCMOS.dig as structural Verilog
module _1_06_aoiCMOS (
  input  B,
  input  A,
  input  D,
  input  C,
  output Z
);

  wire nfet_1_d, nfet_2_d, pfet_1_d;

  PFET pfet_1 (.G(B), .S(1'b1), .D(pfet_1_d));
  PFET pfet_2 (.G(A), .S(1'b1), .D(pfet_1_d));
  NFET nfet_1 (.G(A), .D(nfet_1_d), .S(1'b0));
  NFET nfet_2 (.G(C), .D(nfet_2_d), .S(1'b0));
  PFET pfet_3 (.G(D), .S(pfet_1_d), .D(Z));
  PFET pfet_4 (.G(C), .S(pfet_1_d), .D(Z));
  NFET nfet_3 (.G(B), .D(Z), .S(nfet_1_d));
  NFET nfet_4 (.G(D), .D(Z), .S(nfet_2_d));
endmodule
