// Digital circuit 1.07.multibit.dig as structural Verilog
module _1_07_multibit (
  input  [3:0] A,
  input  [3:0] B,
  output [3:0] X,
  output [3:0] Y
);

  assign X = A ^ B;  // XOr xor_1, 4 bits wide
  xor xor_2 (Y[0], B[0], A[0]);
  xor xor_3 (Y[1], B[1], A[1]);
  xor xor_4 (Y[2], B[2], A[2]);
  xor xor_5 (Y[3], B[3], A[3]);
endmodule

/* Test case eqv:
A B X Y

loop(a,16)
  loop(b,16)
        (a)  (b)  (a^b)  (a^b)
  end loop
end loop
*/
