// Digital circuit 1.08.mux2.dig as structural Verilog
module _1_08_mux2 (
  input  A,
  input  B,
  input  C,
  output Z
);

  wire and_1_out, and_2_out;

  and and_1 (and_1_out, A, B);
  and and_2 (and_2_out, ~A, C);  // And
  or or_1 (Z, and_1_out, and_2_out);
endmodule
