// Digital circuit 1.09.mux8.dig as structural Verilog
module _1_09_mux8 (
  input  S_0,
  input  S_1,
  input  S_2,
  input  A_0,
  input  A_1,
  input  A_2,
  input  A_3,
  input  A_4,
  input  A_5,
  input  A_6,
  input  A_7,
  output Z
);

  wire and_1_out, and_2_out, and_3_out, and_4_out, and_5_out, and_6_out, and_7_out, and_8_out;

  and and_1 (and_1_out, ~S_0, ~S_1, ~S_2, A_0);  // And
  and and_2 (and_2_out, S_0, ~S_1, ~S_2, A_1);  // And
  and and_3 (and_3_out, ~S_0, S_1, ~S_2, A_2);  // And
  and and_4 (and_4_out, S_0, S_1, ~S_2, A_3);  // And
  and and_5 (and_5_out, ~S_0, ~S_1, S_2, A_4);  // And
  and and_6 (and_6_out, S_0, ~S_1, S_2, A_5);  // And
  and and_7 (and_7_out, ~S_0, S_1, S_2, A_6);  // And
  and and_8 (and_8_out, S_0, S_1, S_2, A_7);
  or or_1 (Z, and_1_out, and_2_out, and_3_out, and_4_out, and_5_out, and_6_out, and_7_out, and_8_out);
endmodule

/* Test case t8x9:
S_2 S_1 S_0   A_7 A_6 A_5 A_4 A_3 A_2 A_1 A_0  Z

0 0 0   0 0 0 0 0 0 0 0   0
0 0 0   0 0 0 0 0 0 0 1   1
0 0 0   0 0 0 0 0 0 1 0   0
0 0 0   0 0 0 0 0 1 0 0   0
0 0 0   0 0 0 0 1 0 0 0   0
0 0 0   0 0 0 1 0 0 0 0   0
0 0 0   0 0 1 0 0 0 0 0   0
0 0 0   0 1 0 0 0 0 0 0   0
0 0 0   1 0 0 0 0 0 0 0   0

0 0 1   0 0 0 0 0 0 0 0   0
0 0 1   0 0 0 0 0 0 0 1   0
0 0 1   0 0 0 0 0 0 1 0   1
0 0 1   0 0 0 0 0 1 0 0   0
0 0 1   0 0 0 0 1 0 0 0   0
0 0 1   0 0 0 1 0 0 0 0   0
0 0 1   0 0 1 0 0 0 0 0   0
0 0 1   0 1 0 0 0 0 0 0   0
0 0 1   1 0 0 0 0 0 0 0   0

0 1 0   0 0 0 0 0 0 0 0   0
0 1 0   0 0 0 0 0 0 0 1   0
0 1 0   0 0 0 0 0 0 1 0   0
0 1 0   0 0 0 0 0 1 0 0   1
0 1 0   0 0 0 0 1 0 0 0   0
0 1 0   0 0 0 1 0 0 0 0   0
0 1 0   0 0 1 0 0 0 0 0   0
0 1 0   0 1 0 0 0 0 0 0   0
0 1 0   1 0 0 0 0 0 0 0   0

0 1 1   0 0 0 0 0 0 0 0   0
0 1 1   0 0 0 0 0 0 0 1   0
0 1 1   0 0 0 0 0 0 1 0   0
0 1 1   0 0 0 0 0 1 0 0   0
0 1 1   0 0 0 0 1 0 0 0   1
0 1 1   0 0 0 1 0 0 0 0   0
0 1 1   0 0 1 0 0 0 0 0   0
0 1 1   0 1 0 0 0 0 0 0   0
0 1 1   1 0 0 0 0 0 0 0   0

1 0 0   0 0 0 0 0 0 0 0   0
1 0 0   0 0 0 0 0 0 0 1   0
1 0 0   0 0 0 0 0 0 1 0   0
1 0 0   0 0 0 0 0 1 0 0   0
1 0 0   0 0 0 0 1 0 0 0   0
1 0 0   0 0 0 1 0 0 0 0   1
1 0 0   0 0 1 0 0 0 0 0   0
1 0 0   0 1 0 0 0 0 0 0   0
1 0 0   1 0 0 0 0 0 0 0   0

1 0 1   0 0 0 0 0 0 0 0   0
1 0 1   0 0 0 0 0 0 0 1   0
1 0 1   0 0 0 0 0 0 1 0   0
1 0 1   0 0 0 0 0 1 0 0   0
1 0 1   0 0 0 0 1 0 0 0   0
1 0 1   0 0 0 1 0 0 0 0   0
1 0 1   0 0 1 0 0 0 0 0   1
1 0 1   0 1 0 0 0 0 0 0   0
1 0 1   1 0 0 0 0 0 0 0   0

1 1 0   0 0 0 0 0 0 0 0   0
1 1 0   0 0 0 0 0 0 0 1   0
1 1 0   0 0 0 0 0 0 1 0   0
1 1 0   0 0 0 0 0 1 0 0   0
1 1 0   0 0 0 0 1 0 0 0   0
1 1 0   0 0 0 1 0 0 0 0   0
1 1 0   0 0 1 0 0 0 0 0   0
1 1 0   0 1 0 0 0 0 0 0   1
1 1 0   1 0 0 0 0 0 0 0   0

1 1 1   0 0 0 0 0 0 0 0   0
1 1 1   0 0 0 0 0 0 0 1   0
1 1 1   0 0 0 0 0 0 1 0   0
1 1 1   0 0 0 0 0 1 0 0   0
1 1 1   0 0 0 0 1 0 0 0   0
1 1 1   0 0 0 1 0 0 0 0   0
1 1 1   0 0 1 0 0 0 0 0   0
1 1 1   0 1 0 0 0 0 0 0   0
1 1 1   1 0 0 0 0 0 0 0   1
*/

/* Test case t8x256:
S_2 S_1 S_0   A_7 A_6 A_5 A_4 A_3 A_2 A_1 A_0  Z

loop(s,8)
  loop(a,256)
        bits(3,s) bits(8,a) bits(1,a>>s)
  end loop
end loop
*/
