// Digital circuit 1.10.mux8tr.dig as structural Verilog
module _1_10_mux8tr (
  input  S_0,
  input  S_1,
  input  S_2,
  input  A_0,
  input  A_1,
  input  A_2,
  input  A_3,
  input  A_4,
  input  A_5,
  input  A_6,
  input  A_7,
  output Z
);

  wire fgnfet_1_d, fgnfet_3_d, fgnfet_5_d, fgnfet_7_d, fgnfet_9_d, fgnfet_11_d, not_1_out, not_2_out,
       not_3_out;

  not not_1 (not_1_out, S_0);
  not not_2 (not_2_out, S_1);
  not not_3 (not_3_out, S_2);
  FGNFET fgnfet_1 (.G(not_1_out), .D(fgnfet_1_d), .S(A_0));
  FGNFET fgnfet_2 (.G(S_0), .D(fgnfet_1_d), .S(A_1));
  FGNFET fgnfet_3 (.G(not_1_out), .D(fgnfet_3_d), .S(A_2));
  FGNFET fgnfet_4 (.G(S_0), .D(fgnfet_3_d), .S(A_3));
  FGNFET fgnfet_5 (.G(not_1_out), .D(fgnfet_5_d), .S(A_4));
  FGNFET fgnfet_6 (.G(S_0), .D(fgnfet_5_d), .S(A_5));
  FGNFET fgnfet_7 (.G(not_1_out), .D(fgnfet_7_d), .S(A_6));
  FGNFET fgnfet_8 (.G(S_0), .D(fgnfet_7_d), .S(A_7));
  FGNFET fgnfet_9 (.G(not_2_out), .D(fgnfet_9_d), .S(fgnfet_1_d));
  FGNFET fgnfet_10 (.G(S_1), .D(fgnfet_9_d), .S(fgnfet_3_d));
  FGNFET fgnfet_11 (.G(not_2_out), .D(fgnfet_11_d), .S(fgnfet_5_d));
  FGNFET fgnfet_12 (.G(S_1), .D(fgnfet_11_d), .S(fgnfet_7_d));
  FGNFET fgnfet_13 (.G(not_3_out), .D(Z), .S(fgnfet_9_d));
  FGNFET fgnfet_14 (.G(S_2), .D(Z), .S(fgnfet_11_d));
endmodule

/* Test case t8x9:
S_2 S_1 S_0   A_7 A_6 A_5 A_4 A_3 A_2 A_1 A_0  Z

0 0 0   0 0 0 0 0 0 0 0   0
0 0 0   0 0 0 0 0 0 0 1   1
0 0 0   0 0 0 0 0 0 1 0   0
0 0 0   0 0 0 0 0 1 0 0   0
0 0 0   0 0 0 0 1 0 0 0   0
0 0 0   0 0 0 1 0 0 0 0   0
0 0 0   0 0 1 0 0 0 0 0   0
0 0 0   0 1 0 0 0 0 0 0   0
0 0 0   1 0 0 0 0 0 0 0   0

0 0 1   0 0 0 0 0 0 0 0   0
0 0 1   0 0 0 0 0 0 0 1   0
0 0 1   0 0 0 0 0 0 1 0   1
0 0 1   0 0 0 0 0 1 0 0   0
0 0 1   0 0 0 0 1 0 0 0   0
0 0 1   0 0 0 1 0 0 0 0   0
0 0 1   0 0 1 0 0 0 0 0   0
0 0 1   0 1 0 0 0 0 0 0   0
0 0 1   1 0 0 0 0 0 0 0   0

0 1 0   0 0 0 0 0 0 0 0   0
0 1 0   0 0 0 0 0 0 0 1   0
0 1 0   0 0 0 0 0 0 1 0   0
0 1 0   0 0 0 0 0 1 0 0   1
0 1 0   0 0 0 0 1 0 0 0   0
0 1 0   0 0 0 1 0 0 0 0   0
0 1 0   0 0 1 0 0 0 0 0   0
0 1 0   0 1 0 0 0 0 0 0   0
0 1 0   1 0 0 0 0 0 0 0   0

0 1 1   0 0 0 0 0 0 0 0   0
0 1 1   0 0 0 0 0 0 0 1   0
0 1 1   0 0 0 0 0 0 1 0   0
0 1 1   0 0 0 0 0 1 0 0   0
0 1 1   0 0 0 0 1 0 0 0   1
0 1 1   0 0 0 1 0 0 0 0   0
0 1 1   0 0 1 0 0 0 0 0   0
0 1 1   0 1 0 0 0 0 0 0   0
0 1 1   1 0 0 0 0 0 0 0   0

1 0 0   0 0 0 0 0 0 0 0   0
1 0 0   0 0 0 0 0 0 0 1   0
1 0 0   0 0 0 0 0 0 1 0   0
1 0 0   0 0 0 0 0 1 0 0   0
1 0 0   0 0 0 0 1 0 0 0   0
1 0 0   0 0 0 1 0 0 0 0   1
1 0 0   0 0 1 0 0 0 0 0   0
1 0 0   0 1 0 0 0 0 0 0   0
1 0 0   1 0 0 0 0 0 0 0   0

1 0 1   0 0 0 0 0 0 0 0   0
1 0 1   0 0 0 0 0 0 0 1   0
1 0 1   0 0 0 0 0 0 1 0   0
1 0 1   0 0 0 0 0 1 0 0   0
1 0 1   0 0 0 0 1 0 0 0   0
1 0 1   0 0 0 1 0 0 0 0   0
1 0 1   0 0 1 0 0 0 0 0   1
1 0 1   0 1 0 0 0 0 0 0   0
1 0 1   1 0 0 0 0 0 0 0   0

1 1 0   0 0 0 0 0 0 0 0   0
1 1 0   0 0 0 0 0 0 0 1   0
1 1 0   0 0 0 0 0 0 1 0   0
1 1 0   0 0 0 0 0 1 0 0   0
1 1 0   0 0 0 0 1 0 0 0   0
1 1 0   0 0 0 1 0 0 0 0   0
1 1 0   0 0 1 0 0 0 0 0   0
1 1 0   0 1 0 0 0 0 0 0   1
1 1 0   1 0 0 0 0 0 0 0   0

1 1 1   0 0 0 0 0 0 0 0   0
1 1 1   0 0 0 0 0 0 0 1   0
1 1 1   0 0 0 0 0 0 1 0   0
1 1 1   0 0 0 0 0 1 0 0   0
1 1 1   0 0 0 0 1 0 0 0   0
1 1 1   0 0 0 1 0 0 0 0   0
1 1 1   0 0 1 0 0 0 0 0   0
1 1 1   0 1 0 0 0 0 0 0   0
1 1 1   1 0 0 0 0 0 0 0   1
*/

/* Test case t8x256:
S_2 S_1 S_0   A_7 A_6 A_5 A_4 A_3 A_2 A_1 A_0  Z

loop(s,8)
  loop(a,256)
        bits(3,s) bits(8,a) bits(1,a>>s)
  end loop
end loop
*/
