// Digital circuit 1.13.add4.dig as structural Verilog
module _1_13_add4 (
  input  A_0,
  input  B_0,
  input  C_in,
  input  A_1,
  input  B_1,
  input  A_2,
  input  B_2,
  input  A_3,
  input  B_3,
  output C_out,
  output S_0,
  output S_1,
  output S_2,
  output S_3
);

  wire and_1_out, and_2_out, and_3_out, and_4_out, and_5_out, and_6_out, and_7_out, and_8_out, or_2_out,
       or_3_out, or_4_out, xor_1_out, xor_3_out, xor_5_out, xor_7_out;

  xor xor_1 (xor_1_out, A_3, B_3);
  xor xor_2 (S_3, xor_1_out, or_2_out);
  and and_1 (and_1_out, A_3, B_3);
  and and_2 (and_2_out, xor_1_out, or_2_out);
  or or_1 (C_out, and_1_out, and_2_out);
  xor xor_3 (xor_3_out, A_2, B_2);
  xor xor_4 (S_2, xor_3_out, or_3_out);
  and and_3 (and_3_out, A_2, B_2);
  and and_4 (and_4_out, xor_3_out, or_3_out);
  or or_2 (or_2_out, and_3_out, and_4_out);
  xor xor_5 (xor_5_out, A_1, B_1);
  xor xor_6 (S_1, xor_5_out, or_4_out);
  and and_5 (and_5_out, A_1, B_1);
  and and_6 (and_6_out, xor_5_out, or_4_out);
  or or_3 (or_3_out, and_5_out, and_6_out);
  xor xor_7 (xor_7_out, A_0, B_0);
  xor xor_8 (S_0, xor_7_out, C_in);
  and and_7 (and_7_out, A_0, B_0);
  and and_8 (and_8_out, xor_7_out, C_in);
  or or_4 (or_4_out, and_7_out, and_8_out);
endmodule

/* Test case t16x16:
C_in   A_3 A_2 A_1 A_0   B_3 B_2 B_1 B_0   C_out S_3 S_2 S_1 S_0

loop(a,16)
  loop(b,16)
      0 bits(4,a) bits(4,b) bits(5,a+b)
      1 bits(4,a) bits(4,b) bits(5,a+b+1)
  end loop
end loop
*/
