// Digital circuit 1.14.addsub4.dig as structural Verilog
module _1_14_addsub4 (
  input  A_0,
  input  B_0,
  input  C_in,
  input  A_1,
  input  B_1,
  input  A_2,
  input  B_2,
  input  A_3,
  input  B_3,
  input  invB,
  output C_out,
  output S_0,
  output S_1,
  output S_2,
  output S_3
);

  wire and_1_out, and_2_out, and_3_out, and_4_out, and_5_out, and_6_out, and_7_out, and_8_out, or_2_out,
       or_3_out, or_4_out, xor_1_out, xor_2_out, xor_4_out, xor_5_out, xor_7_out, xor_8_out, xor_10_out,
       xor_11_out;

  xor xor_1 (xor_1_out, B_3, invB);
  xor xor_2 (xor_2_out, A_3, xor_1_out);
  xor xor_3 (S_3, xor_2_out, or_2_out);
  and and_1 (and_1_out, A_3, xor_1_out);
  and and_2 (and_2_out, xor_2_out, or_2_out);
  or or_1 (C_out, and_1_out, and_2_out);
  xor xor_4 (xor_4_out, B_2, invB);
  xor xor_5 (xor_5_out, A_2, xor_4_out);
  xor xor_6 (S_2, xor_5_out, or_3_out);
  and and_3 (and_3_out, A_2, xor_4_out);
  and and_4 (and_4_out, xor_5_out, or_3_out);
  or or_2 (or_2_out, and_3_out, and_4_out);
  xor xor_7 (xor_7_out, B_1, invB);
  xor xor_8 (xor_8_out, A_1, xor_7_out);
  xor xor_9 (S_1, xor_8_out, or_4_out);
  and and_5 (and_5_out, A_1, xor_7_out);
  and and_6 (and_6_out, xor_8_out, or_4_out);
  or or_3 (or_3_out, and_5_out, and_6_out);
  xor xor_10 (xor_10_out, B_0, invB);
  xor xor_11 (xor_11_out, A_0, xor_10_out);
  xor xor_12 (S_0, xor_11_out, C_in);
  and and_7 (and_7_out, A_0, xor_10_out);
  and and_8 (and_8_out, xor_11_out, C_in);
  or or_4 (or_4_out, and_7_out, and_8_out);
endmodule

/* Test case +16x17:
invB  C_in   A_3 A_2 A_1 A_0   B_3 B_2 B_1 B_0   C_out S_3 S_2 S_1 S_0

loop(a,16)
  loop(b,16)
      0 0 bits(4,a) bits(4,b) bits(5,a+b)
      0 1 bits(4,a) bits(4,b) bits(5,a+b+1)
  end loop
end loop
*/

/* Test case -16x16:
invB  C_in   A_3 A_2 A_1 A_0   B_3 B_2 B_1 B_0   C_out S_3 S_2 S_1 S_0

loop(a,16)
  loop(b,16)
      1 0 bits(4,a) bits(4,b) bits(5,(a-b-1)^16)
      1 1 bits(4,a) bits(4,b) bits(5,(a-b)^16)
  end loop
end loop
*/
