// Digital circuit 2.05.rsnand.dig as structural Verilog
module _2_05_rsnand (
  input  reset,
  input  set,
  output Q,
  output Q_2
);

  nand nand_1 (Q, reset, Q_2);
  nand nand_2 (Q_2, Q, set);
endmodule
