// Digital circuit 2.06.dff.dig as structural Verilog
module _2_06_dff (
  input  D,
  input  clock,
  output Q,
  output Q_2
);

  wire nand_1_out, nand_2_out;

  nand nand_1 (nand_1_out, ~D, clock);  // NAnd
  nand nand_2 (nand_2_out, D, clock);
  nand nand_3 (Q, nand_1_out, Q_2);
  nand nand_4 (Q_2, Q, nand_2_out);
endmodule
