// Digital circuit 2.07.latch.dig as structural Verilog
module _2_07_latch (
  input  D,
  input  clock,
  output Q
);

  wire and_1_out, and_2_out;

  and and_1 (and_1_out, D, clock);
  and and_2 (and_2_out, Q, ~clock);  // And
  or or_1 (Q, and_1_out, and_2_out);
endmodule
