// Digital circuit 2.08.edgedff.dig as structural Verilog
module _2_08_edgedff (
  input  D,
  input  clock,
  output Q
);

  wire and_1_out, and_2_out, and_3_out, and_4_out, or_1_out;

  and and_1 (and_1_out, D, ~clock);  // And
  and and_2 (and_2_out, or_1_out, clock);
  or or_1 (or_1_out, and_1_out, and_2_out);
  and and_3 (and_3_out, or_1_out, clock);
  and and_4 (and_4_out, Q, ~clock);  // And
  or or_2 (Q, and_3_out, and_4_out);
endmodule
