// Digital circuit 2.09.reg.dig as structural Verilog
module _2_09_reg (
  input  D,
  input  En,
  input  clock,
  output Q
);

  wire and_1_out, and_2_out, and_3_out, and_4_out, and_5_out, and_6_out, or_1_out, or_2_out;

  and and_1 (and_1_out, D, En);
  and and_2 (and_2_out, Q, ~En);  // And
  or or_1 (or_1_out, and_1_out, and_2_out);
  and and_3 (and_3_out, or_1_out, ~clock);  // And
  and and_4 (and_4_out, or_2_out, clock);
  or or_2 (or_2_out, and_3_out, and_4_out);
  and and_5 (and_5_out, or_2_out, clock);
  and and_6 (and_6_out, Q, ~clock);  // And
  or or_3 (Q, and_5_out, and_6_out);
endmodule
