// Digital circuit 3.02.mcpu_pc.dig as structural Verilog
module _3_02_mcpu_pc (
  input  clock
);

  wire [13:0] add_1_s, PC_q;

  Add #(.Bits(14)) add_1 (.a(PC_q), .b({14{1'b0}}), .c_i(1'b1), .s(add_1_s));  // open: c_o
  Register #(.Bits(14)) PC (.D(add_1_s), .C(clock), .en(1'b1), .Q(PC_q));
endmodule
