// Digital circuit 3.03.mcpu_mem.dig as structural Verilog
module _3_03_mcpu_mem (
  input  clock
);

  wire [13:0] add_1_s, PC_q;
  wire [15:0] ramdualaccess_1_d2;

  Add #(.Bits(14)) add_1 (.a(PC_q), .b({14{1'b0}}), .c_i(1'b1), .s(add_1_s));  // open: c_o
  Register #(.Bits(14)) PC (.D(add_1_s), .C(clock), .en(1'b1), .Q(PC_q));
  RAMDualAccess #(.AddrBits(14), .Bits(16)) ramdualaccess_1 (
    .str(1'b0), .C(clock), .ld(1'b1), .A1({14{1'b0}}), .Din1({16{1'b0}}), .A2(PC_q), .D2(ramdualaccess_1_d2));  // open: D1
endmodule
