// Digital circuit 3.04.mcpu_jcc.dig as structural Verilog
module _3_04_mcpu_jcc (
  input  clock,
  input  C,
  output [13:0] PC
);

  wire and_1_out;
  wire [13:0] add_1_s, multiplexer_1_out;
  wire [15:0] ramdualaccess_1_d1, ramdualaccess_1_d2;

  Add #(.Bits(14)) add_1 (.a(PC), .b({14{1'b0}}), .c_i(1'b1), .s(add_1_s));  // open: c_o
  Multiplexer #(.Bits(14)) multiplexer_1 (
    .sel(and_1_out), .in_0(add_1_s), .in_1(ramdualaccess_1_d2[13:0]), .out(multiplexer_1_out));
  Register #(.Bits(14)) u_PC (.D(multiplexer_1_out), .C(clock), .en(1'b1), .Q(PC));
  and and_1 (and_1_out, ramdualaccess_1_d2[14], ramdualaccess_1_d2[15], ~C);  // And
  RAMDualAccess #(.AddrBits(14), .isProgramMemory("true"), .Bits(16)) ramdualaccess_1 (
    .str(1'b0), .C(clock), .ld(1'b1), .A1(ramdualaccess_1_d2[13:0]), .Din1({16{1'b0}}), .A2(PC),
    .D1(ramdualaccess_1_d1), .D2(ramdualaccess_1_d2));
endmodule

/* Test case JCC:
clock C PC
program(0x0000, 0xC006, 0xC001, 0xC008)
0 1 0
C 1 1
C 1 2
C 0 1
C 1 2
C 0 1
C 0 6
*/
