// Digital circuit 3.06.mcpu_jcc_nor_sta.dig as structural Verilog
module _3_06_mcpu_jcc_nor_sta (
  input  clock,
  input  C,
  output [13:0] PC,
  output [15:0] Acc
);

  wire and_1_out, and_2_out, and_3_out;
  wire [13:0] add_1_s, multiplexer_1_out;
  wire [15:0] nor_1_out, ramdualaccess_1_d1, ramdualaccess_1_d2;

  Add #(.Bits(14)) add_1 (.a(PC), .b({14{1'b0}}), .c_i(1'b1), .s(add_1_s));  // open: c_o
  Multiplexer #(.Bits(14)) multiplexer_1 (
    .sel(and_1_out), .in_0(add_1_s), .in_1(ramdualaccess_1_d2[13:0]), .out(multiplexer_1_out));
  Register #(.Bits(14)) u_PC (.D(multiplexer_1_out), .C(clock), .en(1'b1), .Q(PC));
  and and_1 (and_1_out, ramdualaccess_1_d2[14], ramdualaccess_1_d2[15], ~C);  // And
  assign nor_1_out = ~(ramdualaccess_1_d1 | Acc);  // NOr nor_1, 16 bits wide
  and and_2 (and_2_out, ~ramdualaccess_1_d2[14], ~ramdualaccess_1_d2[15]);  // And
  Register #(.Bits(16)) u_Acc (.D(nor_1_out), .C(clock), .en(and_2_out), .Q(Acc));
  and and_3 (and_3_out, ~ramdualaccess_1_d2[14], ramdualaccess_1_d2[15]);  // And
  RAMDualAccess #(.AddrBits(14), .isProgramMemory("true"), .Bits(16)) ramdualaccess_1 (
    .str(and_3_out), .C(clock), .ld(1'b1), .A1(ramdualaccess_1_d2[13:0]), .Din1(Acc), .A2(PC),
    .D1(ramdualaccess_1_d1), .D2(ramdualaccess_1_d2));
endmodule

/* Test case JCC:
clock C PC
program(0x0000, 0xC006, 0xC001, 0xC008)
0 1 0
C 1 1
C 1 2
C 0 1
C 1 2
C 0 1
C 0 6
*/

/* Test case NOR:
clock Acc
program(0x0004, 0x0000, 0x0001, 0x0002, 0xFFFF)
0 0
C 0
C 0xFFFB
C 4
C 0xFFFA
*/

/* Test case STA:
clock Acc
program(0x0004,0x8004,0xC000,0x0000,0xFFFF)
0 0
C 0
C 0
C 0
C 0xFFFF
C 0xFFFF
C 0xFFFF
C 0
C 0
C 0
C 0xFFFF
*/
