// Digital circuit 3.08.mcputerm.dig as structural Verilog
module _3_08_mcputerm (
  input  clock,
  output [13:0] PC,
  output [15:0] Acc
);

  wire add_2_c_o, and_1_out, and_2_out, and_3_out, and_4_out, and_5_out, and_6_out, C_q, not_1_out;
  wire [13:0] add_1_s, multiplexer_1_out;
  wire [15:0] add_2_s, keyboard_1_d, multiplexer_2_out, multiplexer_3_out, nor_1_out, ramdualaccess_1_d1,
       ramdualaccess_1_d2;

  and and_1 (and_1_out, ~ramdualaccess_1_d2[15], add_2_c_o);  // And
  Add #(.Bits(14)) add_1 (.a(PC), .b({14{1'b0}}), .c_i(1'b1), .s(add_1_s));  // open: c_o
  Register C (.D(and_1_out), .C(clock), .en(ramdualaccess_1_d2[14]), .Q(C_q));
  Multiplexer #(.Bits(14)) multiplexer_1 (
    .sel(and_2_out), .in_0(add_1_s), .in_1(ramdualaccess_1_d2[13:0]), .out(multiplexer_1_out));
  Register #(.Bits(14)) u_PC (.D(multiplexer_1_out), .C(clock), .en(1'b1), .Q(PC));
  and and_2 (and_2_out, ramdualaccess_1_d2[14], ramdualaccess_1_d2[15], ~C_q);  // And
  assign nor_1_out = ~(multiplexer_3_out | Acc);  // NOr nor_1, 16 bits wide
  Add #(.Bits(16)) add_2 (.a(multiplexer_3_out), .b(Acc), .c_i(1'b0), .s(add_2_s), .c_o(add_2_c_o));
  not not_1 (not_1_out, ramdualaccess_1_d2[15]);
  Multiplexer #(.Bits(16)) multiplexer_2 (
    .sel(ramdualaccess_1_d2[14]), .in_0(nor_1_out), .in_1(add_2_s), .out(multiplexer_2_out));
  Register #(.Bits(16)) u_Acc (.D(multiplexer_2_out), .C(clock), .en(not_1_out), .Q(Acc));
  and and_3 (and_3_out, ~ramdualaccess_1_d2[14], ramdualaccess_1_d2[15]);  // And
  and and_4 (and_4_out, ramdualaccess_1_d2[0], ramdualaccess_1_d2[1], ramdualaccess_1_d2[2], ramdualaccess_1_d2[3], ramdualaccess_1_d2[4], ramdualaccess_1_d2[5], ramdualaccess_1_d2[6], ramdualaccess_1_d2[7], ramdualaccess_1_d2[8], ramdualaccess_1_d2[9], ramdualaccess_1_d2[10], ramdualaccess_1_d2[11], ramdualaccess_1_d2[12], ramdualaccess_1_d2[13]);
  RAMDualAccess #(.AddrBits(14), .isProgramMemory("true"), .Bits(16)) ramdualaccess_1 (
    .str(and_3_out), .C(clock), .ld(1'b1), .A1(ramdualaccess_1_d2[13:0]), .Din1(Acc), .A2(PC),
    .D1(ramdualaccess_1_d1), .D2(ramdualaccess_1_d2));
  and and_5 (and_5_out, and_3_out, and_4_out);
  and and_6 (and_6_out, ~and_3_out, and_4_out);  // And
  Terminal terminal_1 (.D(Acc), .C(clock), .en(and_5_out));
  Keyboard keyboard_1 (.C(clock), .en(and_6_out), .D(keyboard_1_d));  // open: av
  Multiplexer #(.Bits(16)) multiplexer_3 (
    .sel(and_4_out), .in_0(ramdualaccess_1_d1), .in_1(keyboard_1_d), .out(multiplexer_3_out));

  // Notes on the sheet:
  //   clock: Hz: 2147483647
endmodule

/* Test case ADD:
clock Acc
program(0x4002,0xC000,0x0001)
0 0
C 1
C 1
C 2
C 2
C 3
C 3
C 4
*/

/* Test case JCC:
clock PC
program(0x0000, 0xC003, 0xC001, 0xC002)
0 0
C 1
C 3
C 2
C 1
C 3
C 2
*/

/* Test case NOR:
clock Acc
program(0x0004, 0x0000, 0x0001, 0x0002, 0xFFFF)
0 0
C 0
C 0xFFFB
C 4
C 0xFFFA
*/

/* Test case STA:
clock Acc
program(0x0004,0x8004,0xC000,0x0000,0xFFFF)
0 0
C 0
C 0
C 0
C 0xFFFF
C 0xFFFF
C 0xFFFF
C 0
C 0
C 0
C 0xFFFF
*/
