// Digital circuit 3.09.drv_pc.dig as structural Verilog
module _3_09_drv_pc (
  input  clock,
  output [31:0] PC
);

  wire [31:0] add_1_s, multiplexer_1_out, ramdualaccess_1_d1, ramdualaccess_1_d2;

  Add #(.Bits(32)) add_1 (.a(PC), .b(32'h4), .c_i(1'b0), .s(add_1_s));  // open: c_o
  Multiplexer #(.Bits(32)) multiplexer_1 (.sel(1'b0), .in_0(add_1_s), .in_1({32{1'b0}}), .out(multiplexer_1_out));
  Register #(.Bits(32)) u_PC (.D(multiplexer_1_out), .C(clock), .en(1'b1), .Q(PC));
  RAMDualAccess #(.AddrBits(21), .isProgramMemory("true"), .Bits(32)) ramdualaccess_1 (
    .str(1'b1), .C(clock), .ld(1'b1), .A1({21{1'b0}}), .Din1({32{1'b0}}), .A2(PC[22:2]),
    .D1(ramdualaccess_1_d1), .D2(ramdualaccess_1_d2));

  // Notes on the sheet:
  //   clock: Hz: 2147483647
endmodule
