// Digital circuit 3.10.drv_jal.dig as structural Verilog
module _3_10_drv_jal (
  input  clock,
  output [31:0] PC
);

  wire and_1_out, and_2_out;
  wire [7:0] ramdualaccess_1_d2_2;
  wire [31:0] add_1_s, add_2_s, multiplexer_1_out, ramdualaccess_1_d1, ramdualaccess_1_d2;

  Add #(.Bits(32)) add_1 (
    .a(PC),
    .b({{12{ramdualaccess_1_d2[31]}}, ramdualaccess_1_d2_2, ramdualaccess_1_d2[20], ramdualaccess_1_d2[30:21], 1'b0}),
    .c_i(1'b0), .s(add_1_s));  // open: c_o
  Add #(.Bits(32)) add_2 (.a(PC), .b(32'h4), .c_i(1'b0), .s(add_2_s));  // open: c_o
  Multiplexer #(.Bits(32)) multiplexer_1 (.sel(and_2_out), .in_0(add_2_s), .in_1(add_1_s), .out(multiplexer_1_out));
  Register #(.Bits(32)) u_PC (.D(multiplexer_1_out), .C(clock), .en(1'b1), .Q(PC));
  and and_1 (and_1_out, ramdualaccess_1_d2[0], ramdualaccess_1_d2[1]);
  and and_2 (and_2_out, and_1_out, ramdualaccess_1_d2[2], ramdualaccess_1_d2[3], ~ramdualaccess_1_d2[4], ramdualaccess_1_d2[5], ramdualaccess_1_d2[6]);  // And
  RAMDualAccess #(.AddrBits(21), .isProgramMemory("true"), .Bits(32)) ramdualaccess_1 (
    .str(1'b1), .C(clock), .ld(1'b1), .A1({21{1'b0}}), .Din1({32{1'b0}}), .A2(PC[22:2]),
    .D1(ramdualaccess_1_d1), .D2({ramdualaccess_1_d2[31:20], ramdualaccess_1_d2_2, ramdualaccess_1_d2[11:0]}));

  // Notes on the sheet:
  //   clock: Hz: 2147483647
endmodule

/* Test case JAL:
clock PC
program(0x00000000,0xFFDFFFEF)
0 0
C 4
C 0
C 4
C 0
*/
