// Digital circuit 3.11.drv_jal_op_opimm.dig as structural Verilog
module _3_11_drv_jal_op_opimm (
  input  clock
);

  wire and_1_out, and_2_out, and_3_out, and_4_out;
  wire [7:0] ramdualaccess_1_d2_2;
  wire [20:0] PC_q_2;
  wire [31:0] add_1_s, add_2_s, multiplexer_1_out, PC_q, ramdualaccess_1_d1, ramdualaccess_1_d2;

  Add #(.Bits(32)) add_1 (
    .a({PC_q[31:23], PC_q_2, PC_q[1:0]}),
    .b({{12{ramdualaccess_1_d2[31]}}, ramdualaccess_1_d2_2, ramdualaccess_1_d2[20], ramdualaccess_1_d2[30:21], 1'b0}),
    .c_i(1'b0), .s(add_1_s));  // open: c_o
  Add #(.Bits(32)) add_2 (.a({PC_q[31:23], PC_q_2, PC_q[1:0]}), .b(32'h4), .c_i(1'b0), .s(add_2_s));  // open: c_o
  Multiplexer #(.Bits(32)) multiplexer_1 (.sel(and_2_out), .in_0(add_2_s), .in_1(add_1_s), .out(multiplexer_1_out));
  Register #(.Bits(32)) PC (.D(multiplexer_1_out), .C(clock), .en(1'b1), .Q({PC_q[31:23], PC_q_2, PC_q[1:0]}));
  // Probe PC on {PC_q[31:23], PC_q_2, PC_q[1:0]}
  and and_1 (and_1_out, ramdualaccess_1_d2[0], ramdualaccess_1_d2[1]);
  and and_2 (and_2_out, and_1_out, ramdualaccess_1_d2[2], ramdualaccess_1_d2[3], ~ramdualaccess_1_d2[4], ramdualaccess_1_d2[5], ramdualaccess_1_d2[6]);  // And
  and and_3 (and_3_out, and_1_out, ~ramdualaccess_1_d2[2], ~ramdualaccess_1_d2[3], ramdualaccess_1_d2[4], ramdualaccess_1_d2[5], ~ramdualaccess_1_d2[6]);  // And
  and and_4 (and_4_out, and_1_out, ~ramdualaccess_1_d2[2], ~ramdualaccess_1_d2[3], ramdualaccess_1_d2[4], ~ramdualaccess_1_d2[5], ~ramdualaccess_1_d2[6]);  // And
  // Probe OP on and_3_out
  // Probe OP-IMM on and_4_out
  // Probe JAL on and_2_out
  RAMDualAccess #(.AddrBits(21), .isProgramMemory("true"), .Bits(32)) ramdualaccess_1 (
    .str(1'b1), .C(clock), .ld(1'b1), .A1({21{1'b0}}), .Din1({32{1'b0}}), .A2(PC_q_2),
    .D1(ramdualaccess_1_d1), .D2({ramdualaccess_1_d2[31:20], ramdualaccess_1_d2_2, ramdualaccess_1_d2[11:0]}));

  // Notes on the sheet:
  //   clock: Hz: 2147483647
endmodule

/* Test case JAL:
clock PC JAL
program(0x00000013,0xFFDFFFEF)
0 0 0
C 4 1
C 0 0
C 4 1
C 0 0
*/

/* Test case ADD:
clock OP
program(0x00100093,0x001080B3, 0xFFDF06F)
#   1 0000 93001000 	 addi x1,zero,1
#   2 0004 B3801000 	loop:add x1,x1,x1
#   3 0008 6FF0DFFF 	 jal zero,loop
0 0
C 0
C 1
C 0
C 1
C 0
*/

/* Test case ADDI:
clock PC
0 0
*/
