// Digital circuit 3.12.drv_jal_op_opimm_reg.dig as structural Verilog
module _3_12_drv_jal_op_opimm_reg (
  input  clock,
  input  [4:0] rs1,
  input  [4:0] rs2,
  input  [4:0] rd,
  input  wrReg,
  input  [31:0] dIn,
  output [31:0] s1,
  output [31:0] s2
);

  wire and_1_out, and_3_out, and_4_out, and_5_out, and_6_out, and_7_out, and_8_out, and_9_out, and_10_out,
       and_11_out, and_12_out, and_13_out, and_14_out, and_15_out, and_16_out, and_17_out, and_18_out,
       and_19_out, and_20_out, and_21_out, and_22_out, and_23_out, and_24_out, and_25_out, and_26_out,
       and_27_out, and_28_out, and_29_out, and_30_out, and_31_out, and_32_out, and_33_out, and_34_out,
       and_35_out, and_36_out, and_37_out, and_38_out, and_39_out, and_40_out;
  wire [7:0] ramdualaccess_1_d2_2;
  wire [20:0] PC_q_2;
  wire [31:0] add_1_s, add_2_s, multiplexer_1_out, multiplexer_2_out, multiplexer_3_out, multiplexer_4_out,
       multiplexer_5_out, multiplexer_6_out, multiplexer_7_out, multiplexer_8_out, multiplexer_11_out, PC_q,
       ramdualaccess_1_d1, ramdualaccess_1_d2, register_1_q, register_2_q, register_3_q, register_4_q,
       register_5_q, register_6_q, register_7_q, register_8_q, register_9_q, register_10_q, register_11_q,
       register_12_q, register_13_q, register_14_q, register_15_q, register_16_q, register_17_q,
       register_18_q, register_19_q, register_20_q, register_21_q, register_22_q, register_23_q,
       register_24_q, register_25_q, register_26_q, register_27_q, register_28_q, register_29_q,
       register_30_q, register_31_q;

  and and_1 (and_1_out, wrReg, ~rd[3], ~rd[4]);  // And
  // And and_2 has open pins: In_1=and_1_out, In_2=rd[0], In_3=rd[1], In_4=rd[2], out=open
  and and_3 (and_3_out, and_1_out, rd[0], ~rd[1], ~rd[2]);  // And
  and and_4 (and_4_out, and_1_out, ~rd[0], rd[1], ~rd[2]);  // And
  and and_5 (and_5_out, and_1_out, rd[0], rd[1], ~rd[2]);  // And
  and and_6 (and_6_out, and_1_out, ~rd[0], ~rd[1], rd[2]);  // And
  and and_7 (and_7_out, and_1_out, rd[0], ~rd[1], rd[2]);  // And
  and and_8 (and_8_out, and_1_out, ~rd[0], rd[1], rd[2]);  // And
  and and_9 (and_9_out, and_1_out, rd[0], rd[1], rd[2]);
  Register #(.Bits(32)) register_1 (.D(dIn), .C(clock), .en(and_3_out), .Q(register_1_q));
  Register #(.Bits(32)) register_2 (.D(dIn), .C(clock), .en(and_4_out), .Q(register_2_q));
  Register #(.Bits(32)) register_3 (.D(dIn), .C(clock), .en(and_5_out), .Q(register_3_q));
  Register #(.Bits(32)) register_4 (.D(dIn), .C(clock), .en(and_6_out), .Q(register_4_q));
  Register #(.Bits(32)) register_5 (.D(dIn), .C(clock), .en(and_7_out), .Q(register_5_q));
  Register #(.Bits(32)) register_6 (.D(dIn), .C(clock), .en(and_8_out), .Q(register_6_q));
  Register #(.Bits(32)) register_7 (.D(dIn), .C(clock), .en(and_9_out), .Q(register_7_q));
  and and_10 (and_10_out, wrReg, rd[3], ~rd[4]);  // And
  Multiplexer #(.Selector_Bits(3), .Bits(32)) multiplexer_1 (
    .sel(rs1[2:0]), .in_0({32{1'b0}}), .in_1(register_1_q), .in_2(register_2_q), .in_3(register_3_q),
    .in_4(register_4_q), .in_5(register_5_q), .in_6(register_6_q), .in_7(register_7_q),
    .out(multiplexer_1_out));
  Multiplexer #(.Selector_Bits(3), .Bits(32)) multiplexer_2 (
    .sel(rs2[2:0]), .in_0({32{1'b0}}), .in_1(register_1_q), .in_2(register_2_q), .in_3(register_3_q),
    .in_4(register_4_q), .in_5(register_5_q), .in_6(register_6_q), .in_7(register_7_q),
    .out(multiplexer_2_out));
  and and_11 (and_11_out, and_10_out, ~rd[0], ~rd[1], ~rd[2]);  // And
  and and_12 (and_12_out, and_10_out, rd[0], ~rd[1], ~rd[2]);  // And
  and and_13 (and_13_out, and_10_out, ~rd[0], rd[1], ~rd[2]);  // And
  and and_14 (and_14_out, and_10_out, rd[0], rd[1], ~rd[2]);  // And
  and and_15 (and_15_out, and_10_out, ~rd[0], ~rd[1], rd[2]);  // And
  and and_16 (and_16_out, and_10_out, rd[0], ~rd[1], rd[2]);  // And
  and and_17 (and_17_out, and_10_out, ~rd[0], rd[1], rd[2]);  // And
  and and_18 (and_18_out, and_10_out, rd[0], rd[1], rd[2]);
  Register #(.Bits(32)) register_8 (.D(dIn), .C(clock), .en(and_11_out), .Q(register_8_q));
  Register #(.Bits(32)) register_9 (.D(dIn), .C(clock), .en(and_12_out), .Q(register_9_q));
  Register #(.Bits(32)) register_10 (.D(dIn), .C(clock), .en(and_13_out), .Q(register_10_q));
  Register #(.Bits(32)) register_11 (.D(dIn), .C(clock), .en(and_14_out), .Q(register_11_q));
  Register #(.Bits(32)) register_12 (.D(dIn), .C(clock), .en(and_15_out), .Q(register_12_q));
  Register #(.Bits(32)) register_13 (.D(dIn), .C(clock), .en(and_16_out), .Q(register_13_q));
  Register #(.Bits(32)) register_14 (.D(dIn), .C(clock), .en(and_17_out), .Q(register_14_q));
  Register #(.Bits(32)) register_15 (.D(dIn), .C(clock), .en(and_18_out), .Q(register_15_q));
  and and_19 (and_19_out, wrReg, ~rd[3], rd[4]);  // And
  Multiplexer #(.Selector_Bits(3), .Bits(32)) multiplexer_3 (
    .sel(rs1[2:0]), .in_0(register_8_q), .in_1(register_9_q), .in_2(register_10_q), .in_3(register_11_q),
    .in_4(register_12_q), .in_5(register_13_q), .in_6(register_14_q), .in_7(register_15_q),
    .out(multiplexer_3_out));
  Multiplexer #(.Selector_Bits(3), .Bits(32)) multiplexer_4 (
    .sel(rs2[2:0]), .in_0(register_8_q), .in_1(register_9_q), .in_2(register_10_q), .in_3(register_11_q),
    .in_4(register_12_q), .in_5(register_13_q), .in_6(register_14_q), .in_7(register_15_q),
    .out(multiplexer_4_out));
  and and_20 (and_20_out, and_19_out, ~rd[0], ~rd[1], ~rd[2]);  // And
  and and_21 (and_21_out, and_19_out, rd[0], ~rd[1], ~rd[2]);  // And
  and and_22 (and_22_out, and_19_out, ~rd[0], rd[1], ~rd[2]);  // And
  and and_23 (and_23_out, and_19_out, rd[0], rd[1], ~rd[2]);  // And
  and and_24 (and_24_out, and_19_out, ~rd[0], ~rd[1], rd[2]);  // And
  and and_25 (and_25_out, and_19_out, rd[0], ~rd[1], rd[2]);  // And
  and and_26 (and_26_out, and_19_out, ~rd[0], rd[1], rd[2]);  // And
  and and_27 (and_27_out, and_19_out, rd[0], rd[1], rd[2]);
  Register #(.Bits(32)) register_16 (.D(dIn), .C(clock), .en(and_20_out), .Q(register_16_q));
  Register #(.Bits(32)) register_17 (.D(dIn), .C(clock), .en(and_21_out), .Q(register_17_q));
  Register #(.Bits(32)) register_18 (.D(dIn), .C(clock), .en(and_22_out), .Q(register_18_q));
  Register #(.Bits(32)) register_19 (.D(dIn), .C(clock), .en(and_23_out), .Q(register_19_q));
  Register #(.Bits(32)) register_20 (.D(dIn), .C(clock), .en(and_24_out), .Q(register_20_q));
  Register #(.Bits(32)) register_21 (.D(dIn), .C(clock), .en(and_25_out), .Q(register_21_q));
  Register #(.Bits(32)) register_22 (.D(dIn), .C(clock), .en(and_26_out), .Q(register_22_q));
  Register #(.Bits(32)) register_23 (.D(dIn), .C(clock), .en(and_27_out), .Q(register_23_q));
  and and_28 (and_28_out, wrReg, rd[3], rd[4]);
  Multiplexer #(.Bits(32), .Selector_Bits(3)) multiplexer_5 (
    .sel(rs1[2:0]), .in_0(register_16_q), .in_1(register_17_q), .in_2(register_18_q), .in_3(register_19_q),
    .in_4(register_20_q), .in_5(register_21_q), .in_6(register_22_q), .in_7(register_23_q),
    .out(multiplexer_5_out));
  Multiplexer #(.Selector_Bits(3), .Bits(32)) multiplexer_6 (
    .sel(rs2[2:0]), .in_0(register_16_q), .in_1(register_17_q), .in_2(register_18_q), .in_3(register_19_q),
    .in_4(register_20_q), .in_5(register_21_q), .in_6(register_22_q), .in_7(register_23_q),
    .out(multiplexer_6_out));
  and and_29 (and_29_out, and_28_out, ~rd[0], ~rd[1], ~rd[2]);  // And
  and and_30 (and_30_out, and_28_out, rd[0], ~rd[1], ~rd[2]);  // And
  and and_31 (and_31_out, and_28_out, ~rd[0], rd[1], ~rd[2]);  // And
  and and_32 (and_32_out, and_28_out, rd[0], rd[1], ~rd[2]);  // And
  and and_33 (and_33_out, and_28_out, ~rd[0], ~rd[1], rd[2]);  // And
  and and_34 (and_34_out, and_28_out, rd[0], ~rd[1], rd[2]);  // And
  and and_35 (and_35_out, and_28_out, ~rd[0], rd[1], rd[2]);  // And
  and and_36 (and_36_out, and_28_out, rd[0], rd[1], rd[2]);
  Register #(.Bits(32)) register_24 (.D(dIn), .C(clock), .en(and_29_out), .Q(register_24_q));
  Register #(.Bits(32)) register_25 (.D(dIn), .C(clock), .en(and_30_out), .Q(register_25_q));
  Register #(.Bits(32)) register_26 (.D(dIn), .C(clock), .en(and_31_out), .Q(register_26_q));
  Register #(.Bits(32)) register_27 (.D(dIn), .C(clock), .en(and_32_out), .Q(register_27_q));
  Register #(.Bits(32)) register_28 (.D(dIn), .C(clock), .en(and_33_out), .Q(register_28_q));
  Register #(.Bits(32)) register_29 (.D(dIn), .C(clock), .en(and_34_out), .Q(register_29_q));
  Register #(.Bits(32)) register_30 (.D(dIn), .C(clock), .en(and_35_out), .Q(register_30_q));
  Register #(.Bits(32)) register_31 (.D(dIn), .C(clock), .en(and_36_out), .Q(register_31_q));
  Multiplexer #(.Selector_Bits(3), .Bits(32)) multiplexer_7 (
    .sel(rs1[2:0]), .in_0(register_24_q), .in_1(register_25_q), .in_2(register_26_q), .in_3(register_27_q),
    .in_4(register_28_q), .in_5(register_29_q), .in_6(register_30_q), .in_7(register_31_q),
    .out(multiplexer_7_out));
  Multiplexer #(.Selector_Bits(3), .Bits(32)) multiplexer_8 (
    .sel(rs2[2:0]), .in_0(register_24_q), .in_1(register_25_q), .in_2(register_26_q), .in_3(register_27_q),
    .in_4(register_28_q), .in_5(register_29_q), .in_6(register_30_q), .in_7(register_31_q),
    .out(multiplexer_8_out));
  Multiplexer #(.Bits(32), .Selector_Bits(2)) multiplexer_9 (
    .sel(rs1[4:3]), .in_0(multiplexer_1_out), .in_1(multiplexer_3_out), .in_2(multiplexer_5_out),
    .in_3(multiplexer_7_out), .out(s1));
  Multiplexer #(.Selector_Bits(2), .Bits(32)) multiplexer_10 (
    .sel(rs2[4:3]), .in_0(multiplexer_2_out), .in_1(multiplexer_4_out), .in_2(multiplexer_6_out),
    .in_3(multiplexer_8_out), .out(s2));
  Add #(.Bits(32)) add_1 (
    .a({PC_q[31:23], PC_q_2, PC_q[1:0]}),
    .b({{12{ramdualaccess_1_d2[31]}}, ramdualaccess_1_d2_2, ramdualaccess_1_d2[20], ramdualaccess_1_d2[30:21], 1'b0}),
    .c_i(1'b0), .s(add_1_s));  // open: c_o
  Add #(.Bits(32)) add_2 (.a({PC_q[31:23], PC_q_2, PC_q[1:0]}), .b(32'h4), .c_i(1'b0), .s(add_2_s));  // open: c_o
  Multiplexer #(.Bits(32)) multiplexer_11 (.sel(and_38_out), .in_0(add_2_s), .in_1(add_1_s), .out(multiplexer_11_out));
  Register #(.Bits(32)) PC (.D(multiplexer_11_out), .C(clock), .en(1'b1), .Q({PC_q[31:23], PC_q_2, PC_q[1:0]}));
  // Probe PC on {PC_q[31:23], PC_q_2, PC_q[1:0]}
  and and_37 (and_37_out, ramdualaccess_1_d2[0], ramdualaccess_1_d2[1]);
  and and_38 (and_38_out, and_37_out, ramdualaccess_1_d2[2], ramdualaccess_1_d2[3], ~ramdualaccess_1_d2[4], ramdualaccess_1_d2[5], ramdualaccess_1_d2[6]);  // And
  and and_39 (and_39_out, and_37_out, ~ramdualaccess_1_d2[2], ~ramdualaccess_1_d2[3], ramdualaccess_1_d2[4], ramdualaccess_1_d2[5], ~ramdualaccess_1_d2[6]);  // And
  and and_40 (and_40_out, and_37_out, ~ramdualaccess_1_d2[2], ~ramdualaccess_1_d2[3], ramdualaccess_1_d2[4], ~ramdualaccess_1_d2[5], ~ramdualaccess_1_d2[6]);  // And
  // Probe OP on and_39_out
  // Probe OP-IMM on and_40_out
  // Probe JAL on and_38_out
  RAMDualAccess #(.AddrBits(21), .isProgramMemory("true"), .Bits(32)) ramdualaccess_1 (
    .str(1'b1), .C(clock), .ld(1'b1), .A1({21{1'b0}}), .Din1({32{1'b0}}), .A2(PC_q_2),
    .D1(ramdualaccess_1_d1), .D2({ramdualaccess_1_d2[31:20], ramdualaccess_1_d2_2, ramdualaccess_1_d2[11:0]}));

  // Notes on the sheet:
  //   clock: Hz: 2147483647
endmodule

/* Test case JAL:
clock PC JAL
program(0x00000013,0xFFDFFFEF)
0 0 0
C 4 1
C 0 0
C 4 1
C 0 0
*/

/* Test case ADD:
clock PC OP
program(0x00100093,0x001080B3, 0xFFDF06F)
#   1 0000 93001000 	 addi x1,zero,1
#   2 0004 B3801000 	loop:add x1,x1,x1
#   3 0008 6FF0DFFF 	 jal zero,loop
0 0 0
C 4 1
C 8 0
C C 0
C 10 1
C 14 0
*/

/* Test case ADDI:
clock PC
0 0
*/
