// Digital circuit 3.15.ltTest.dig as structural Verilog
module _3_15_ltTest (
  input  A_0,
  input  B_2,
  input  B_1,
  input  B_0,
  input  A_1,
  input  A_2,
  output S2,
  output C2,
  output C1,
  output V,
  output LT,
  output LTU,
  output S1,
  output S0
);

  wire add_3_c_o, not_1_out, not_2_out, not_3_out;

  not not_1 (not_1_out, B_2);
  not not_2 (not_2_out, B_1);
  not not_3 (not_3_out, B_0);
  Add add_1 (.a(A_2), .b(not_1_out), .c_i(C1), .s(S2), .c_o(C2));
  Add add_2 (.a(A_1), .b(not_2_out), .c_i(add_3_c_o), .s(S1), .c_o(C1));
  Add add_3 (.a(A_0), .b(not_3_out), .c_i(1'b1), .s(S0), .c_o(add_3_c_o));
  xor xor_1 (V, C2, C1);
  xor xor_2 (LT, V, S2);
  not not_4 (LTU, C2);
endmodule

/* Test case LTU:
A_2 A_1 A_0  B_2 B_1 B_0   LTU

loop(a,8)
  loop(b,8)
      bits(3,a) bits(3,b) bits(1, a<b)
  end loop
end loop
*/

/* Test case LT:
A_2 A_1 A_0  B_2 B_1 B_0   LT

loop(a,8)
  loop(b,8)
      bits(3,a) bits(3,b) bits(1, (7&(a+4)) < (7&(b+4)))
  end loop
end loop
*/
