// Digital circuit 3.18.shftTest.dig as structural Verilog
module _3_18_shftTest (
  input  [7:0] D,
  input  [2:0] shft,
  input  sign,
  output [7:0] R,
  output [7:0] Z
);

  wire [3:3] and_1_out;
  wire [7:0] multiplexer_1_out, multiplexer_2_out, multiplexer_3_out, multiplexer_4_out;

  and and_1 (and_1_out[3], D[7], sign);
  Multiplexer #(.Bits(8)) multiplexer_1 (.sel(shft[0]), .in_0(D), .in_1({D[6:0], 1'b0}), .out(multiplexer_1_out));
  Multiplexer #(.Bits(8)) multiplexer_2 (
    .sel(shft[0]), .in_0(D), .in_1({and_1_out[3], D[7:1]}), .out(multiplexer_2_out));
  Multiplexer #(.Bits(8)) multiplexer_3 (
    .sel(shft[1]), .in_0(multiplexer_1_out), .in_1({multiplexer_1_out[5:0], 2'b00}), .out(multiplexer_3_out));
  Multiplexer #(.Bits(8)) multiplexer_4 (
    .sel(shft[1]), .in_0(multiplexer_2_out), .in_1({{2{and_1_out[3]}}, multiplexer_2_out[7:2]}),
    .out(multiplexer_4_out));
  Multiplexer #(.Bits(8)) multiplexer_5 (
    .sel(shft[2]), .in_0(multiplexer_3_out), .in_1({multiplexer_3_out[3:0], 4'b0000}), .out(R));
  Multiplexer #(.Bits(8)) multiplexer_6 (
    .sel(shft[2]), .in_0(multiplexer_4_out), .in_1({{4{and_1_out[3]}}, multiplexer_4_out[7:4]}), .out(Z));
endmodule

/* Test case shift:
D sign shft R Z
loop(shft,8)
  loop(D,256)
    (D) 0 (shft) ((D)<<(shft)) ((D)>>(shft))
    (D) 1 (shft) ((D)<<(shft)) (((D)>>(shft))|ite(D&0x80,0xFF<<(8-shft),0))
  end loop
end loop
*/
