// Digital circuit 3.23.drv.dig as structural Verilog
module _3_23_drv (
  input  clock
);

  wire add_2_c_o, add_3_c_o, add_3_s, and_1_out, and_3_out, and_4_out, and_5_out, and_6_out, and_7_out,
       and_8_out, and_9_out, and_10_out, and_11_out, and_12_out, and_13_out, and_14_out, and_15_out,
       and_16_out, and_17_out, and_18_out, and_19_out, and_20_out, and_21_out, and_22_out, and_23_out,
       and_24_out, and_25_out, and_26_out, and_27_out, and_28_out, and_29_out, and_30_out, and_31_out,
       and_32_out, and_33_out, and_34_out, and_35_out, and_36_out, and_40_out, and_41_out, and_42_out,
       and_43_out, and_44_out, and_45_out, and_46_out, and_47_out, and_48_out, and_49_out, and_50_out,
       and_51_out, and_52_out, and_53_out, and_54_out, and_55_out, and_57_out, and_58_out, and_60_out,
       and_61_out, and_63_out, and_64_out, and_66_out, and_67_out, multiplexer_32_out, nor_1_out, not_4_out,
       not_5_out, not_6_out, not_7_out, or_2_out, or_3_out, or_4_out, or_5_out, or_6_out, or_7_out, or_8_out,
       or_9_out, or_10_out, xor_2_out;
  wire [0:0] not_3_out, xor_3_out;
  wire [1:0] add_4_s, mem2_d1_2, mem3_d1, multiplexer_13_out;
  wire [2:0] mem1_d1, mem2_d1, mem2_d1_3;
  wire [6:0] mem0_d1;
  wire [7:0] mem0_d2, mem1_d2, mem2_d2, mem3_d2, multiplexer_33_out, multiplexer_34_out, multiplexer_35_out,
       multiplexer_36_out, multiplexer_37_out, multiplexer_38_out, multiplexer_39_out, multiplexer_40_out,
       multiplexer_41_out, multiplexer_42_out, multiplexer_43_out;
  wire [7:7] and_56_out, and_59_out, and_62_out, and_65_out;
  wire [15:0] keyboard_1_d;
  wire [20:0] add_4_s_2;
  wire [31:0] add_1_s, add_5_s, add_6_s, and_38_out, mem3_d1_2, multiplexer_1_out, multiplexer_2_out,
       multiplexer_3_out, multiplexer_4_out, multiplexer_5_out, multiplexer_6_out, multiplexer_7_out,
       multiplexer_8_out, multiplexer_9_out, multiplexer_10_out, multiplexer_11_out, multiplexer_13_out_2,
       multiplexer_14_out, multiplexer_15_out, multiplexer_16_out, multiplexer_17_out, multiplexer_18_out,
       multiplexer_19_out, multiplexer_20_out, multiplexer_21_out, multiplexer_22_out, multiplexer_23_out,
       multiplexer_24_out, multiplexer_25_out, multiplexer_26_out, multiplexer_27_out, multiplexer_28_out,
       multiplexer_29_out, multiplexer_30_out, multiplexer_31_out, multiplexer_44_out, not_1_out, not_2_out,
       or_1_out, PC_q, register_1_q, register_2_q, register_3_q, register_4_q, register_5_q, register_6_q,
       register_7_q, register_8_q, register_9_q, register_10_q, register_11_q, register_12_q, register_13_q,
       register_14_q, register_15_q, register_16_q, register_17_q, register_18_q, register_19_q,
       register_20_q, register_21_q, register_22_q, register_23_q, register_24_q, register_25_q,
       register_26_q, register_27_q, register_28_q, register_29_q, register_30_q, register_31_q, xor_1_out;
  wire [31:2] multiplexer_12_out;
  wire [31:23] add_4_s_3;
  wire [31:30] multiplexer_12_out_2;

  // Probe rs1 on {mem2_d1_2, mem2_d1}
  // Probe rs2 on {mem3_d1, mem2_d1_3}
  // Probe rd on mem3_d1_2[4:0]
  // Probe wrReg on nor_1_out
  and and_1 (and_1_out, nor_1_out, ~mem3_d1_2[3], ~mem3_d1_2[4]);  // And
  // And and_2 has open pins: In_1=and_1_out, In_2=mem3_d1_2[0], In_3=mem3_d1_2[1], In_4=mem3_d1_2[2], out=open
  and and_3 (and_3_out, and_1_out, mem3_d1_2[0], ~mem3_d1_2[1], ~mem3_d1_2[2]);  // And
  and and_4 (and_4_out, and_1_out, ~mem3_d1_2[0], mem3_d1_2[1], ~mem3_d1_2[2]);  // And
  and and_5 (and_5_out, and_1_out, mem3_d1_2[0], mem3_d1_2[1], ~mem3_d1_2[2]);  // And
  and and_6 (and_6_out, and_1_out, ~mem3_d1_2[0], ~mem3_d1_2[1], mem3_d1_2[2]);  // And
  and and_7 (and_7_out, and_1_out, mem3_d1_2[0], ~mem3_d1_2[1], mem3_d1_2[2]);  // And
  and and_8 (and_8_out, and_1_out, ~mem3_d1_2[0], mem3_d1_2[1], mem3_d1_2[2]);  // And
  and and_9 (and_9_out, and_1_out, mem3_d1_2[0], mem3_d1_2[1], mem3_d1_2[2]);
  Register #(.Bits(32)) register_1 (.D(multiplexer_31_out), .C(clock), .en(and_3_out), .Q(register_1_q));
  Register #(.Bits(32)) register_2 (.D(multiplexer_31_out), .C(clock), .en(and_4_out), .Q(register_2_q));
  Register #(.Bits(32)) register_3 (.D(multiplexer_31_out), .C(clock), .en(and_5_out), .Q(register_3_q));
  Register #(.Bits(32)) register_4 (.D(multiplexer_31_out), .C(clock), .en(and_6_out), .Q(register_4_q));
  Register #(.Bits(32)) register_5 (.D(multiplexer_31_out), .C(clock), .en(and_7_out), .Q(register_5_q));
  Register #(.Bits(32)) register_6 (.D(multiplexer_31_out), .C(clock), .en(and_8_out), .Q(register_6_q));
  Register #(.Bits(32)) register_7 (.D(multiplexer_31_out), .C(clock), .en(and_9_out), .Q(register_7_q));
  and and_10 (and_10_out, nor_1_out, mem3_d1_2[3], ~mem3_d1_2[4]);  // And
  Multiplexer #(.Selector_Bits(3), .Bits(32)) multiplexer_1 (
    .sel(mem2_d1), .in_0({32{1'b0}}), .in_1(register_1_q), .in_2(register_2_q), .in_3(register_3_q),
    .in_4(register_4_q), .in_5(register_5_q), .in_6(register_6_q), .in_7(register_7_q),
    .out(multiplexer_1_out));
  Multiplexer #(.Selector_Bits(3), .Bits(32)) multiplexer_2 (
    .sel(mem2_d1_3), .in_0({32{1'b0}}), .in_1(register_1_q), .in_2(register_2_q), .in_3(register_3_q),
    .in_4(register_4_q), .in_5(register_5_q), .in_6(register_6_q), .in_7(register_7_q),
    .out(multiplexer_2_out));
  and and_11 (and_11_out, and_10_out, ~mem3_d1_2[0], ~mem3_d1_2[1], ~mem3_d1_2[2]);  // And
  and and_12 (and_12_out, and_10_out, mem3_d1_2[0], ~mem3_d1_2[1], ~mem3_d1_2[2]);  // And
  and and_13 (and_13_out, and_10_out, ~mem3_d1_2[0], mem3_d1_2[1], ~mem3_d1_2[2]);  // And
  and and_14 (and_14_out, and_10_out, mem3_d1_2[0], mem3_d1_2[1], ~mem3_d1_2[2]);  // And
  and and_15 (and_15_out, and_10_out, ~mem3_d1_2[0], ~mem3_d1_2[1], mem3_d1_2[2]);  // And
  and and_16 (and_16_out, and_10_out, mem3_d1_2[0], ~mem3_d1_2[1], mem3_d1_2[2]);  // And
  and and_17 (and_17_out, and_10_out, ~mem3_d1_2[0], mem3_d1_2[1], mem3_d1_2[2]);  // And
  and and_18 (and_18_out, and_10_out, mem3_d1_2[0], mem3_d1_2[1], mem3_d1_2[2]);
  Register #(.Bits(32)) register_8 (.D(multiplexer_31_out), .C(clock), .en(and_11_out), .Q(register_8_q));
  Register #(.Bits(32)) register_9 (.D(multiplexer_31_out), .C(clock), .en(and_12_out), .Q(register_9_q));
  Register #(.Bits(32)) register_10 (.D(multiplexer_31_out), .C(clock), .en(and_13_out), .Q(register_10_q));
  Register #(.Bits(32)) register_11 (.D(multiplexer_31_out), .C(clock), .en(and_14_out), .Q(register_11_q));
  Register #(.Bits(32)) register_12 (.D(multiplexer_31_out), .C(clock), .en(and_15_out), .Q(register_12_q));
  Register #(.Bits(32)) register_13 (.D(multiplexer_31_out), .C(clock), .en(and_16_out), .Q(register_13_q));
  Register #(.Bits(32)) register_14 (.D(multiplexer_31_out), .C(clock), .en(and_17_out), .Q(register_14_q));
  Register #(.Bits(32)) register_15 (.D(multiplexer_31_out), .C(clock), .en(and_18_out), .Q(register_15_q));
  and and_19 (and_19_out, nor_1_out, ~mem3_d1_2[3], mem3_d1_2[4]);  // And
  Multiplexer #(.Selector_Bits(3), .Bits(32)) multiplexer_3 (
    .sel(mem2_d1), .in_0(register_8_q), .in_1(register_9_q), .in_2(register_10_q), .in_3(register_11_q),
    .in_4(register_12_q), .in_5(register_13_q), .in_6(register_14_q), .in_7(register_15_q),
    .out(multiplexer_3_out));
  Multiplexer #(.Selector_Bits(3), .Bits(32)) multiplexer_4 (
    .sel(mem2_d1_3), .in_0(register_8_q), .in_1(register_9_q), .in_2(register_10_q), .in_3(register_11_q),
    .in_4(register_12_q), .in_5(register_13_q), .in_6(register_14_q), .in_7(register_15_q),
    .out(multiplexer_4_out));
  and and_20 (and_20_out, and_19_out, ~mem3_d1_2[0], ~mem3_d1_2[1], ~mem3_d1_2[2]);  // And
  and and_21 (and_21_out, and_19_out, mem3_d1_2[0], ~mem3_d1_2[1], ~mem3_d1_2[2]);  // And
  and and_22 (and_22_out, and_19_out, ~mem3_d1_2[0], mem3_d1_2[1], ~mem3_d1_2[2]);  // And
  and and_23 (and_23_out, and_19_out, mem3_d1_2[0], mem3_d1_2[1], ~mem3_d1_2[2]);  // And
  and and_24 (and_24_out, and_19_out, ~mem3_d1_2[0], ~mem3_d1_2[1], mem3_d1_2[2]);  // And
  and and_25 (and_25_out, and_19_out, mem3_d1_2[0], ~mem3_d1_2[1], mem3_d1_2[2]);  // And
  and and_26 (and_26_out, and_19_out, ~mem3_d1_2[0], mem3_d1_2[1], mem3_d1_2[2]);  // And
  and and_27 (and_27_out, and_19_out, mem3_d1_2[0], mem3_d1_2[1], mem3_d1_2[2]);
  Register #(.Bits(32)) register_16 (.D(multiplexer_31_out), .C(clock), .en(and_20_out), .Q(register_16_q));
  Register #(.Bits(32)) register_17 (.D(multiplexer_31_out), .C(clock), .en(and_21_out), .Q(register_17_q));
  Register #(.Bits(32)) register_18 (.D(multiplexer_31_out), .C(clock), .en(and_22_out), .Q(register_18_q));
  Register #(.Bits(32)) register_19 (.D(multiplexer_31_out), .C(clock), .en(and_23_out), .Q(register_19_q));
  Register #(.Bits(32)) register_20 (.D(multiplexer_31_out), .C(clock), .en(and_24_out), .Q(register_20_q));
  Register #(.Bits(32)) register_21 (.D(multiplexer_31_out), .C(clock), .en(and_25_out), .Q(register_21_q));
  Register #(.Bits(32)) register_22 (.D(multiplexer_31_out), .C(clock), .en(and_26_out), .Q(register_22_q));
  Register #(.Bits(32)) register_23 (.D(multiplexer_31_out), .C(clock), .en(and_27_out), .Q(register_23_q));
  and and_28 (and_28_out, nor_1_out, mem3_d1_2[3], mem3_d1_2[4]);
  Multiplexer #(.Selector_Bits(3), .Bits(32)) multiplexer_5 (
    .sel(mem2_d1), .in_0(register_16_q), .in_1(register_17_q), .in_2(register_18_q), .in_3(register_19_q),
    .in_4(register_20_q), .in_5(register_21_q), .in_6(register_22_q), .in_7(register_23_q),
    .out(multiplexer_5_out));
  Multiplexer #(.Selector_Bits(3), .Bits(32)) multiplexer_6 (
    .sel(mem2_d1_3), .in_0(register_16_q), .in_1(register_17_q), .in_2(register_18_q), .in_3(register_19_q),
    .in_4(register_20_q), .in_5(register_21_q), .in_6(register_22_q), .in_7(register_23_q),
    .out(multiplexer_6_out));
  and and_29 (and_29_out, and_28_out, ~mem3_d1_2[0], ~mem3_d1_2[1], ~mem3_d1_2[2]);  // And
  and and_30 (and_30_out, and_28_out, mem3_d1_2[0], ~mem3_d1_2[1], ~mem3_d1_2[2]);  // And
  and and_31 (and_31_out, and_28_out, ~mem3_d1_2[0], mem3_d1_2[1], ~mem3_d1_2[2]);  // And
  and and_32 (and_32_out, and_28_out, mem3_d1_2[0], mem3_d1_2[1], ~mem3_d1_2[2]);  // And
  and and_33 (and_33_out, and_28_out, ~mem3_d1_2[0], ~mem3_d1_2[1], mem3_d1_2[2]);  // And
  and and_34 (and_34_out, and_28_out, mem3_d1_2[0], ~mem3_d1_2[1], mem3_d1_2[2]);  // And
  and and_35 (and_35_out, and_28_out, ~mem3_d1_2[0], mem3_d1_2[1], mem3_d1_2[2]);  // And
  and and_36 (and_36_out, and_28_out, mem3_d1_2[0], mem3_d1_2[1], mem3_d1_2[2]);
  Register #(.Bits(32)) register_24 (.D(multiplexer_31_out), .C(clock), .en(and_29_out), .Q(register_24_q));
  Register #(.Bits(32)) register_25 (.D(multiplexer_31_out), .C(clock), .en(and_30_out), .Q(register_25_q));
  Register #(.Bits(32)) register_26 (.D(multiplexer_31_out), .C(clock), .en(and_31_out), .Q(register_26_q));
  Register #(.Bits(32)) register_27 (.D(multiplexer_31_out), .C(clock), .en(and_32_out), .Q(register_27_q));
  Register #(.Bits(32)) register_28 (.D(multiplexer_31_out), .C(clock), .en(and_33_out), .Q(register_28_q));
  Register #(.Bits(32)) register_29 (.D(multiplexer_31_out), .C(clock), .en(and_34_out), .Q(register_29_q));
  Register #(.Bits(32)) register_30 (.D(multiplexer_31_out), .C(clock), .en(and_35_out), .Q(register_30_q));
  Register #(.Bits(32)) register_31 (.D(multiplexer_31_out), .C(clock), .en(and_36_out), .Q(register_31_q));
  Multiplexer #(.Selector_Bits(3), .Bits(32)) multiplexer_7 (
    .sel(mem2_d1), .in_0(register_24_q), .in_1(register_25_q), .in_2(register_26_q), .in_3(register_27_q),
    .in_4(register_28_q), .in_5(register_29_q), .in_6(register_30_q), .in_7(register_31_q),
    .out(multiplexer_7_out));
  Multiplexer #(.Selector_Bits(3), .Bits(32)) multiplexer_8 (
    .sel(mem2_d1_3), .in_0(register_24_q), .in_1(register_25_q), .in_2(register_26_q), .in_3(register_27_q),
    .in_4(register_28_q), .in_5(register_29_q), .in_6(register_30_q), .in_7(register_31_q),
    .out(multiplexer_8_out));
  Multiplexer #(.Selector_Bits(2), .Bits(32)) multiplexer_9 (
    .sel(mem2_d1_2), .in_0(multiplexer_1_out), .in_1(multiplexer_3_out), .in_2(multiplexer_5_out),
    .in_3(multiplexer_7_out), .out(multiplexer_9_out));
  Multiplexer #(.Selector_Bits(2), .Bits(32)) multiplexer_10 (
    .sel(mem3_d1), .in_0(multiplexer_2_out), .in_1(multiplexer_4_out), .in_2(multiplexer_6_out),
    .in_3(multiplexer_8_out), .out(multiplexer_10_out));
  // Probe s2 on multiplexer_10_out
  and and_37 (multiplexer_13_out_2[31], multiplexer_9_out[31], and_40_out);
  // Probe s1 on multiplexer_9_out
  Multiplexer #(.Bits(32)) multiplexer_11 (
    .sel(or_7_out), .in_0(multiplexer_10_out), .in_1(multiplexer_14_out), .out(multiplexer_11_out));
  Multiplexer #(.Bits(32)) multiplexer_12 (
    .sel(multiplexer_11_out[0]), .in_0(multiplexer_9_out), .in_1({multiplexer_9_out[30:0], 1'b0}),
    .out({multiplexer_12_out_2, multiplexer_12_out}));
  Multiplexer #(.Bits(32)) multiplexer_13 (
    .sel(multiplexer_11_out[0]), .in_0(multiplexer_9_out),
    .in_1({multiplexer_13_out_2[31], multiplexer_9_out[31:1]}),
    .out({multiplexer_13_out_2[29:0], multiplexer_13_out}));
  Multiplexer #(.Bits(32)) multiplexer_14 (
    .sel(and_50_out), .in_0({{21{mem3_d1_2[31]}}, mem3_d1_2[10:5], mem3_d1, mem2_d1_3}),
    .in_1({{21{mem3_d1_2[31]}}, mem3_d1_2[10:0]}), .out(multiplexer_14_out));
  // Probe immS on {{21{mem3_d1_2[31]}}, mem3_d1_2[10:0]}
  assign not_1_out = ~multiplexer_11_out;  // Not not_1, 32 bits wide
  Multiplexer #(.Bits(32)) multiplexer_15 (
    .sel(multiplexer_11_out[1]), .in_0({multiplexer_12_out_2, multiplexer_12_out}),
    .in_1({multiplexer_12_out, 2'b00}), .out(multiplexer_15_out));
  Multiplexer #(.Bits(32)) multiplexer_16 (
    .sel(multiplexer_11_out[1]), .in_0({multiplexer_13_out_2[29:0], multiplexer_13_out}),
    .in_1({{2{multiplexer_13_out_2[31]}}, multiplexer_13_out_2[29:0]}), .out(multiplexer_16_out));
  assign xor_1_out = multiplexer_9_out ^ multiplexer_11_out;  // XOr xor_1, 32 bits wide
  assign or_1_out = multiplexer_9_out | multiplexer_11_out;  // Or or_1, 32 bits wide
  assign and_38_out = multiplexer_9_out & multiplexer_11_out;  // And and_38, 32 bits wide
  // Probe immBr on {{20{mem3_d1_2[31]}}, mem3_d1_2[0], mem3_d1_2[10:1], 1'b0}
  assign not_2_out = ~multiplexer_11_out;  // Not not_2, 32 bits wide
  // Probe immUI on {mem3_d1_2[31], mem3_d1_2[10:5], mem3_d1, mem2_d1_3, mem2_d1_2, mem2_d1, mem1_d1, {12{1'b0}}}
  Add #(.Bits(32)) add_1 (
    .a(PC_q),
    .b({mem3_d1_2[31], mem3_d1_2[10:5], mem3_d1, mem2_d1_3, mem2_d1_2, mem2_d1, mem1_d1, {12{1'b0}}}),
    .c_i(1'b0), .s(add_1_s));  // open: c_o
  // Probe imm12 on {{21{mem3_d1_2[31]}}, mem3_d1_2[10:5], mem3_d1, mem2_d1_3}
  Multiplexer #(.Bits(32)) multiplexer_17 (
    .sel(and_41_out), .in_0(multiplexer_11_out), .in_1(not_2_out), .out(multiplexer_17_out));
  Add #(.Bits(31)) add_2 (.a(multiplexer_9_out[30:0]), .b(not_1_out[30:0]), .c_i(1'b1), .c_o(add_2_c_o));  // open: s
  Add add_3 (.a(multiplexer_9_out[31]), .b(not_1_out[31]), .c_i(add_2_c_o), .s(add_3_s), .c_o(add_3_c_o));
  Multiplexer #(.Bits(32)) multiplexer_18 (
    .sel(multiplexer_11_out[2]), .in_0(multiplexer_15_out), .in_1({multiplexer_15_out[27:0], 4'b0000}),
    .out(multiplexer_18_out));
  Multiplexer #(.Bits(32)) multiplexer_19 (
    .sel(multiplexer_11_out[2]), .in_0(multiplexer_16_out),
    .in_1({{4{multiplexer_13_out_2[31]}}, multiplexer_16_out[31:4]}), .out(multiplexer_19_out));
  Multiplexer #(.Bits(32)) multiplexer_20 (
    .sel(and_48_out),
    .in_0({mem3_d1_2[31], mem3_d1_2[10:5], mem3_d1, mem2_d1_3, mem2_d1_2, mem2_d1, mem1_d1, {12{1'b0}}}),
    .in_1(add_1_s), .out(multiplexer_20_out));
  // Probe imm20 on {{12{mem3_d1_2[31]}}, mem2_d1_2, mem2_d1, mem1_d1, mem2_d1_3[0], mem3_d1_2[10:5], mem3_d1, mem2_d1_3[2:1], 1'b0}
  Add #(.Bits(32)) add_4 (
    .a(multiplexer_9_out), .b(multiplexer_17_out), .c_i(and_41_out), .s({add_4_s_3, add_4_s_2, add_4_s}));  // open: c_o
  Multiplexer #(.Bits(32)) multiplexer_21 (
    .sel(and_51_out),
    .in_0({{12{mem3_d1_2[31]}}, mem2_d1_2, mem2_d1, mem1_d1, mem2_d1_3[0], mem3_d1_2[10:5], mem3_d1, mem2_d1_3[2:1], 1'b0}),
    .in_1({{20{mem3_d1_2[31]}}, mem3_d1_2[0], mem3_d1_2[10:1], 1'b0}), .out(multiplexer_21_out));
  // And and_39 has open pins: In_1=mem3_d1_2[5], In_2=mem3_d1_2[6], In_3=mem3_d1_2[7], In_4=mem3_d1_2[8], In_5=mem3_d1_2[9], In_6=mem3_d1_2[10], In_7=mem3_d1_2[31], out=open
  and and_40 (and_40_out, ~mem3_d1_2[5], ~mem3_d1_2[6], ~mem3_d1_2[7], ~mem3_d1_2[8], ~mem3_d1_2[9], mem3_d1_2[10], ~mem3_d1_2[31]);  // And
  and and_41 (and_41_out, and_44_out, and_40_out);
  xor xor_2 (xor_2_out, add_2_c_o, add_3_c_o);
  Add #(.Bits(32)) add_5 (.a(PC_q), .b(32'h4), .c_i(1'b0), .s(add_5_s));  // open: c_o
  Add #(.Bits(32)) add_6 (.a(PC_q), .b(multiplexer_21_out), .c_i(1'b0), .s(add_6_s));  // open: c_o
  // Probe funct7 on {mem3_d1_2[31], mem3_d1_2[10:5]}
  // Probe V on xor_2_out
  xor xor_3 (xor_3_out[0], xor_2_out, add_3_s);
  Multiplexer #(.Bits(32)) multiplexer_22 (
    .sel(multiplexer_11_out[3]), .in_0(multiplexer_18_out), .in_1({multiplexer_18_out[23:0], {8{1'b0}}}),
    .out(multiplexer_22_out));
  Multiplexer #(.Bits(32)) multiplexer_23 (
    .sel(multiplexer_11_out[3]), .in_0(multiplexer_19_out),
    .in_1({{8{multiplexer_13_out_2[31]}}, multiplexer_19_out[31:8]}), .out(multiplexer_23_out));
  Multiplexer #(.Bits(32)) multiplexer_24 (
    .sel(or_5_out), .in_0(add_5_s), .in_1(multiplexer_20_out), .out(multiplexer_24_out));
  not not_3 (not_3_out[0], add_3_c_o);
  // Probe pc4 on add_5_s
  // Probe funct3 on mem1_d1
  Multiplexer #(.Selector_Bits(3), .Bits(32)) multiplexer_25 (
    .sel(mem1_d1), .in_0({add_4_s_3, add_4_s_2, add_4_s}), .in_1(multiplexer_28_out),
    .in_2({{31{1'b0}}, xor_3_out[0]}), .in_3({{31{1'b0}}, not_3_out[0]}), .in_4(xor_1_out),
    .in_5(multiplexer_29_out), .in_6(or_1_out), .in_7(and_38_out), .out(multiplexer_25_out));
  // Probe LT on xor_3_out[0]
  // Probe LTU on not_3_out[0]
  Multiplexer #(.Bits(32)) multiplexer_26 (
    .sel(and_46_out), .in_0(add_6_s), .in_1(multiplexer_25_out), .out(multiplexer_26_out));
  Multiplexer #(.Bits(32)) multiplexer_27 (
    .sel(or_4_out), .in_0(add_5_s), .in_1(multiplexer_26_out), .out(multiplexer_27_out));
  // Probe Result on multiplexer_25_out
  Multiplexer #(.Bits(32)) multiplexer_28 (
    .sel(multiplexer_11_out[4]), .in_0(multiplexer_22_out), .in_1({multiplexer_22_out[15:0], {16{1'b0}}}),
    .out(multiplexer_28_out));
  Multiplexer #(.Bits(32)) multiplexer_29 (
    .sel(multiplexer_11_out[4]), .in_0(multiplexer_23_out),
    .in_1({{16{multiplexer_13_out_2[31]}}, multiplexer_23_out[31:16]}), .out(multiplexer_29_out));
  Register #(.Bits(32)) PC (.D(multiplexer_27_out), .C(clock), .en(1'b1), .Q(PC_q));
  // Probe Addr on {add_4_s_3, add_4_s_2, add_4_s}
  Multiplexer #(.Bits(32)) multiplexer_30 (
    .sel(or_6_out), .in_0(multiplexer_25_out), .in_1(multiplexer_24_out), .out(multiplexer_30_out));
  Multiplexer #(.Bits(32)) multiplexer_31 (
    .sel(and_52_out), .in_0(multiplexer_30_out), .in_1(multiplexer_44_out), .out(multiplexer_31_out));
  // Probe PC on PC_q
  not not_4 (not_4_out, or_2_out);
  not not_5 (not_5_out, xor_3_out[0]);
  not not_6 (not_6_out, not_3_out[0]);
  Multiplexer #(.Selector_Bits(3)) multiplexer_32 (
    .sel(mem1_d1), .in_0(not_4_out), .in_1(or_2_out), .in_2(1'b0), .in_3(1'b0), .in_4(xor_3_out[0]),
    .in_5(not_5_out), .in_6(not_3_out[0]), .in_7(not_6_out), .out(multiplexer_32_out));
  or or_2 (or_2_out, xor_1_out[0], xor_1_out[1], xor_1_out[2], xor_1_out[3], xor_1_out[4], xor_1_out[5], xor_1_out[6], xor_1_out[7], xor_1_out[8], xor_1_out[9], xor_1_out[10], xor_1_out[11], xor_1_out[12], xor_1_out[13], xor_1_out[14], xor_1_out[15], xor_1_out[16], xor_1_out[17], xor_1_out[18], xor_1_out[19], xor_1_out[20], xor_1_out[21], xor_1_out[22], xor_1_out[23], xor_1_out[24], xor_1_out[25], xor_1_out[26], xor_1_out[27], xor_1_out[28], xor_1_out[29], xor_1_out[30], xor_1_out[31]);
  and and_42 (and_42_out, mem0_d1[0], mem0_d1[1]);
  and and_43 (and_43_out, and_42_out, mem0_d1[2], mem0_d1[3], ~mem0_d1[4], mem0_d1[5], mem0_d1[6]);  // And
  and and_44 (and_44_out, and_42_out, ~mem0_d1[2], ~mem0_d1[3], mem0_d1[4], mem0_d1[5], ~mem0_d1[6]);  // And
  and and_45 (and_45_out, and_42_out, ~mem0_d1[2], ~mem0_d1[3], mem0_d1[4], ~mem0_d1[5], ~mem0_d1[6]);  // And
  and and_46 (and_46_out, and_42_out, mem0_d1[2], ~mem0_d1[3], ~mem0_d1[4], mem0_d1[5], mem0_d1[6]);  // And
  and and_47 (and_47_out, and_42_out, ~mem0_d1[2], ~mem0_d1[3], ~mem0_d1[4], mem0_d1[5], mem0_d1[6]);  // And
  and and_48 (and_48_out, and_42_out, mem0_d1[2], ~mem0_d1[3], mem0_d1[4], ~mem0_d1[5], ~mem0_d1[6]);  // And
  and and_49 (and_49_out, and_42_out, mem0_d1[2], ~mem0_d1[3], mem0_d1[4], mem0_d1[5], ~mem0_d1[6]);  // And
  // Probe JAL on and_43_out
  // Probe OP on and_44_out
  // Probe OP-IMM on and_45_out
  // Probe AUIPC on and_48_out
  // Probe LUI on and_49_out
  and and_50 (and_50_out, and_42_out, ~mem0_d1[2], ~mem0_d1[3], ~mem0_d1[4], mem0_d1[5], ~mem0_d1[6]);  // And
  // Probe STORE on and_50_out
  // Probe NE on or_2_out
  // Probe JALR on and_46_out
  // Probe branch on and_47_out
  or or_3 (or_3_out, and_45_out, and_46_out);
  or or_4 (or_4_out, and_43_out, and_46_out, and_51_out);
  and and_51 (and_51_out, and_47_out, multiplexer_32_out);
  or or_5 (or_5_out, and_48_out, and_49_out);
  or or_6 (or_6_out, or_5_out, or_4_out);
  nor nor_1 (nor_1_out, and_47_out, and_50_out);
  // Probe LOAD on and_52_out
  and and_52 (and_52_out, and_42_out, ~mem0_d1[2], ~mem0_d1[3], ~mem0_d1[4], ~mem0_d1[5], ~mem0_d1[6]);  // And
  or or_7 (or_7_out, or_3_out, and_52_out, and_50_out);
  and and_53 (and_53_out, add_4_s[0], add_4_s[1]);
  and and_54 (and_54_out, add_4_s[1], mem1_d1[0]);
  Multiplexer #(.Selector_Bits(2), .Bits(8)) multiplexer_33 (
    .sel(mem1_d1[1:0]), .in_0(multiplexer_10_out[7:0]), .in_1(multiplexer_10_out[7:0]),
    .in_2(multiplexer_10_out[7:0]), .in_3(multiplexer_10_out[7:0]), .out(multiplexer_33_out));
  Multiplexer #(.Selector_Bits(2), .Bits(8)) multiplexer_34 (
    .sel(mem1_d1[1:0]), .in_0(multiplexer_10_out[7:0]), .in_1(multiplexer_10_out[15:8]),
    .in_2(multiplexer_10_out[15:8]), .in_3(multiplexer_10_out[7:0]), .out(multiplexer_34_out));
  Multiplexer #(.Selector_Bits(2), .Bits(8)) multiplexer_35 (
    .sel(mem1_d1[1:0]), .in_0(multiplexer_10_out[7:0]), .in_1(multiplexer_10_out[7:0]),
    .in_2(multiplexer_10_out[23:16]), .in_3(multiplexer_10_out[7:0]), .out(multiplexer_35_out));
  Multiplexer #(.Selector_Bits(2), .Bits(8)) multiplexer_36 (
    .sel(mem1_d1[1:0]), .in_0(multiplexer_10_out[7:0]), .in_1(multiplexer_10_out[15:8]),
    .in_2(multiplexer_10_out[31:24]), .in_3(multiplexer_10_out[7:0]), .out(multiplexer_36_out));
  not not_7 (not_7_out, mem1_d1[2]);
  and and_55 (and_55_out, and_50_out, or_8_out);
  or or_8 (or_8_out, and_53_out, and_54_out, mem1_d1[1]);
  RAMDualAccess #(.AddrBits(21), .isProgramMemory("true"), .Bits(8)) mem3 (
    .str(and_55_out), .C(clock), .ld(and_52_out), .A1(add_4_s_2), .Din1(multiplexer_36_out), .A2(PC_q[22:2]),
    .D1({mem3_d1_2[31], mem3_d1_2[10:5], mem3_d1[1]}), .D2(mem3_d2));
  and and_56 (and_56_out[7], mem3_d2[7], not_7_out);
  and and_57 (and_57_out, ~add_4_s[0], add_4_s[1]);  // And
  RAMDualAccess #(.AddrBits(21), .isProgramMemory("true"), .Bits(8)) mem2 (
    .str(and_58_out), .C(clock), .ld(and_52_out), .A1(add_4_s_2), .Din1(multiplexer_35_out), .A2(PC_q[22:2]),
    .D1({mem3_d1[0], mem2_d1_3, mem2_d1_2, mem2_d1[2:1]}), .D2(mem2_d2));
  and and_58 (and_58_out, and_50_out, or_9_out);
  or or_9 (or_9_out, and_57_out, mem1_d1[1]);
  and and_59 (and_59_out[7], mem2_d2[7], not_7_out);
  and and_60 (and_60_out, add_4_s[0], ~add_4_s[1]);  // And
  and and_61 (and_61_out, ~add_4_s[1], mem1_d1[0]);  // And
  RAMDualAccess #(.AddrBits(21), .isProgramMemory("true"), .Bits(8)) mem1 (
    .str(and_63_out), .C(clock), .ld(and_52_out), .A1(add_4_s_2), .Din1(multiplexer_34_out), .A2(PC_q[22:2]),
    .D1({mem2_d1[0], mem1_d1, mem3_d1_2[4:1]}), .D2(mem1_d2));
  and and_62 (and_62_out[7], mem1_d2[7], not_7_out);
  and and_63 (and_63_out, and_50_out, or_10_out);
  or or_10 (or_10_out, and_60_out, and_61_out, mem1_d1[1]);
  and and_64 (and_64_out, and_50_out, ~add_4_s[0], ~add_4_s[1]);  // And
  RAMDualAccess #(.AddrBits(21), .isProgramMemory("true"), .Bits(8)) mem0 (
    .str(and_64_out), .C(clock), .ld(and_52_out), .A1(add_4_s_2), .Din1(multiplexer_33_out), .A2(PC_q[22:2]),
    .D1({mem3_d1_2[0], mem0_d1}), .D2(mem0_d2));
  and and_65 (and_65_out[7], mem0_d2[7], not_7_out);
  Multiplexer #(.Bits(8)) multiplexer_37 (
    .sel(add_4_s[1]), .in_0({8{and_62_out[7]}}), .in_1({8{and_56_out[7]}}), .out(multiplexer_37_out));
  and and_66 (and_66_out, and_50_out, add_4_s_3[31]);
  and and_67 (and_67_out, and_52_out, add_4_s_3[31]);
  Multiplexer #(.Bits(8)) multiplexer_38 (.sel(add_4_s[1]), .in_0(mem1_d2), .in_1(mem3_d2), .out(multiplexer_38_out));
  Terminal terminal_1 (.D(multiplexer_10_out), .C(clock), .en(and_66_out));
  Keyboard keyboard_1 (.C(clock), .en(and_67_out), .D(keyboard_1_d));  // open: av
  Multiplexer #(.Selector_Bits(2), .Bits(8)) multiplexer_39 (
    .sel(add_4_s), .in_0({8{and_65_out[7]}}), .in_1({8{and_62_out[7]}}), .in_2({8{and_59_out[7]}}),
    .in_3({8{and_56_out[7]}}), .out(multiplexer_39_out));
  Multiplexer #(.Selector_Bits(2), .Bits(8)) multiplexer_40 (
    .sel(mem1_d1[1:0]), .in_0(multiplexer_39_out), .in_1(multiplexer_38_out), .in_2(multiplexer_38_out),
    .in_3(multiplexer_38_out), .out(multiplexer_40_out));
  Multiplexer #(.Selector_Bits(2), .Bits(8)) multiplexer_41 (
    .sel(add_4_s), .in_0(mem0_d2), .in_1(mem1_d2), .in_2(mem2_d2), .in_3(mem3_d2), .out(multiplexer_41_out));
  Multiplexer #(.Selector_Bits(2), .Bits(8)) multiplexer_42 (
    .sel(mem1_d1[1:0]), .in_0(multiplexer_39_out), .in_1(multiplexer_37_out), .in_2(mem2_d2), .in_3(mem2_d2),
    .out(multiplexer_42_out));
  Multiplexer #(.Selector_Bits(2), .Bits(8)) multiplexer_43 (
    .sel(mem1_d1[1:0]), .in_0(multiplexer_39_out), .in_1(multiplexer_37_out), .in_2(mem3_d2), .in_3(mem3_d2),
    .out(multiplexer_43_out));
  Multiplexer #(.Bits(32)) multiplexer_44 (
    .sel(and_67_out),
    .in_0({multiplexer_43_out, multiplexer_42_out, multiplexer_40_out, multiplexer_41_out}),
    .in_1({{16{1'b0}}, keyboard_1_d}), .out(multiplexer_44_out));

  // Notes on the sheet:
  //   clock: Hz: 2147483647
endmodule

/* Test case JAL:
clock PC JAL
program(0x00000013,0xFFDFFFEF)
0 0 0
C 4 1
C 0 0
C 4 1
C 0 0
*/

/* Test case ADD:
clock PC OP Result
program(0x00100093,0x001080B3, 0xFFDFF06F)
#   1 0000 93001000 	 addi x1,zero,1
#   2 0004 B3801000 	loop:add x1,x1,x1
#   3 0008 6FF0DFFF 	 jal zero,loop
0 0 0 1
C 4 1 2
C 8 0 X
C 4 1 4
C 8 0 X
C 4 1 8
C 8 0 X
C 4 1 16
C 8 0 X
C 4 1 32
C 8 0 X
C 4 1 64
*/

/* Test case ADDI:
clock PC OP-IMM Result
program(0x07D00093,0x04B08093, 0xF9C08093)
#   1 0000 9300D007 	 addi x1,zero,125
#   2 0004 9380B004 	 addi x1,x1,75
#   3 0008 9380C0F9 	 addi x1,x1,-100
0 0 1 125
C 4 1 200
C 8 1 100
*/

/* Test case JALR:
clock PC Result
program(0x008000EF,0x0000006F,0x00100313,0x00008167)
#   1 0000 EF008000 	 jal x1,funct
#   2 0004 6F000000 	halt:jal zero,halt
#   3 0008 13031000 	funct:addi x6,zero,1
#   4 000c 67810000 	 jalr x2,0(x1)
0 0 X
C 8 1
C 12 4
C 4 X
C 4 X
*/

/* Test case branch:
clock PC Result LT LTU NE
program(0x00200313,0x00730663,0x006003B3,0xFE730AE3,0x00034063,0xFFF30313,0xFE63DCE3,0xFF5FF06F)
#   1 0000 13032000 	start:addi x6,zero,2
#   2 0004 63067300 	 beq x6,x7,halt
#   3 0008 B3036000 	 add x7,zero,x6
#   4 000c E30A73FE 	 beq x6,x7,start
#   5 0010 63400300 	halt:blt x6,zero,halt
#   6 0014 1303F3FF 	 addi x6,x6,-1
#   7 0018 E3DC63FE 	 bge x7,x6,halt
#   8 001c 6FF05FFF 	 jal zero,halt
0 0 2 X X X
C 4 X X X X
C 8 2 X X X
C 12 X X X X
C 0 2 X X X
C 4 X X X X
C 16 X X X X
C 20 1 X X X
C 24 X X X X
C 16 X X X X
C 20 0 X X X
C 24 X X X X
C 16 X X X X
C 20 (-1) X X X
C 24 X X X X
C 16 X X X X
C 16 X X X X
C 16 X X X X
*/

/* Test case LUI AUIPC:
clock PC Result
program(0x12345337,0x00030333,0x12345317,0x00030333)
#   1 0000 37533412 	 lui x6,0x12345
#   2 0004 33030300 	 add x6,x6,zero
#   3 0008 17533412 	 auipc x6,0x12345
#   4 000c 33030300 	 add x6,x6,zero
0 0 X
C 4 0x12345000
C 8 X
C 12 0x12345008 
*/

/* Test case SUB:
clock PC OP Result
program(0x02A00313,0x05F00393,0x40730433,0x408304B3)
  # 1 0000 1303A002 	 addi x6,zero,42
  # 2 0004 9303F005 	 addi x7,zero,95
  # 3 0008 33047340 	 sub x8,x6,x7
  # 4 000c B3048340 	 sub x9,x6,x8
0 0 0 42
C 4 0 95
C 8 1 0xFFFFFFCB
C 12 1 95
*/

/* Test case logic:
clock PC Result
program(0x03600313,0x06300393,0x00734433,0x00737433,0x00736433,0x00F34413,0x00F37413,0x00F36413)
#   1 0000 13036003 	 addi x6,zero,0x36
#   2 0004 93033006 	 addi x7,zero,0x63
#   3 0008 33447300 	 xor x8,x6,x7
#   4 000c 33747300 	 and x8,x6,x7
#   5 0010 33647300 	 or x8,x6,x7
#   6 0014 1344F300 	 xori x8,x6,0x0f
#   7 0018 1374F300 	 and x8,x6,0x0f
#   8 001c 1364F300 	 or x8,x6,0x0f
0 0 0x36
C 4 0x63
C 8 0x55
C 12 0x22
C 16 0x77
C 20 0x39
C 24 0x06
C 28 0x3F
*/

/* Test case fibonacci:
clock PC OP Result
program(0x00100313,0x00100393,0x00730433,0x00038333,0x000403B3,0xFF5FF06F)
#   1 0000 13031000 	 addi x6,zero,1
#   2 0004 93031000 	 addi x7,zero,1
#   3 0008 33047300 	fib:add x8,x6,x7
#   4 000c 33830300 	 add x6,x7,zero
#   5 0010 B3030400 	 add x7,x8,zero
#   6 0014 6FF05FFF 	 jal zero,fib
0 0 0 1
C 4 0 1
C 8 1 2
C 12 1 1
C 16 1 2
C 20 0 X
C 8 1 3
C 12 1 2
C 16 1 3
C 20 0 X
C 8 1 5
C 12 1 3
C 16 1 5
C 20 0 X
C 8 1 8
C 12 1 5
C 16 1 8
C 20 0 X
C 8 1 13
C 12 1 8
C 16 1 13
C 20 0 X
*/

/* Test case cmp:
clock PC Result
program(0x00300313,0x00732433,0x00733433,0xFFB32413,0xFFB33413,0x00532413)
#   1 0000 13033000 	 addi x6,zero,3
#   2 0004 33247300 	 slt x8,x6,x7
#   3 0008 33347300 	 sltu x8,x6,x7
#   4 000C 1324B3FF 	 slti x8,x6,-5
#   5 0010 1334B3FF 	 sltiu x8,x6,-5
#   6 0014 13245300 	 slti x8,x6,5
0 0 3
C 4 0
C 8 0
C 12 0
C 16 1
C 20 1
*/

/* Test case shift:
clock PC Result
program(0x08100313,0x00300393,0x01831413,0x407454B3,0x41045493,0x007454B3,0x01045493,0x007414B3)
#   1 0000 13031008 	 addi x6,zero,0x81
#   2 0004 93033000 	 addi x7,zero,3
#   3 0008 13148301 	 slli x8,x6,24
#   4 000c B3547440 	 sra x9,x8,x7
#   5 0010 93540441 	 srai x9,x8,16
#   6 0014 B3547400 	 srl x9,x8,x7
#   7 0018 93540401 	 srli x9,x8,16
#   8 001c B3147400 	 sll x9,x8,x7
0 0 0x81
C 4 3
C 8 0x81000000
C 12 0xF0200000
C 16 0xFFFF8100
C 20 0x10200000
C 24 0x00008100
C 28 0x08000000
*/

/* Test case SW LW:
clock PC Addr Result imm12 immS s1
program(0x00400313,0x00432383,0x000383B3,0xFFC32403,0x00040433,0x0A702023,0x0A002483,0x000484B3)
#   1 0000 13034000 	 addi x6,zero,4
#   2 0004 83234300 	 lw x7,4(x6)
#   3 0008 B3830300 	 add x7,x7,zero
#   4 000c 0324C3FF 	 lw x8,-4(x6)
#   5 0010 33040400 	 add x8,x8,zero
#   6 0014 2320700A 	 sw x7,160(zero)
#   7 0018 8324000A 	 lw x9,160(zero)
#   8 001c B3840400 	 add x9,x9,zero
0 0 X 4 X X X
C 4 8 X X X X
C 8 X 0x000383B3 X X X
C 12 0 X X X X
C 16 X 0x00400313 X X X
C 20 160 X X X 0
C 24 160 X X X 0
C 28 X 0x000383B3 X X X
*/
